// Logisim project 32_bit_cpu.circ as structural Verilog
module L_1_bit_half_adder_0ae93a57 (
  input  _0,
  input  _1,
  output Sum,
  output Carry
);

  xor xor_1 (Sum, _0, _1);
  buf and_1 (Carry, _0);  // AND_Gate
endmodule

module main (
  input  Power_button,
  input  [31:0] PERIPH_DATA_IN,
  input  [31:0] BOOT_ROM_DATA,
  input  CLK,
  input  [31:0] MEM_DATA_IN,
  output MEM_WRITE_ENABLE,
  output QUADBYTE,
  output [31:0] PERIPH_DATA_OUT,
  output [21:0] BOOT_ROM_ADDR,
  output [21:0] PERIPH_ADDR_OUT,
  output [31:0] MEM_DATA_OUT,
  output [22:0] MEM_ADDR_OUT
);

  wire and_1_out, and_2_out, and_3_out, buffer_1_out, control_unit_1_alu_enable,
       control_unit_1_bootstrap_state, control_unit_1_mem_addr_emit, control_unit_1_next_instruction_trigger,
       control_unit_1_pc_write_enable, control_unit_1_reg_write_enable_out, not_1_out, not_2_out, not_3_out,
       not_4_out, not_5_out, not_6_out, or_1_out, or_2_out, pull_resistor_4_node;
  wire [1:0] counter_1_q;
  wire [1:1] pull_resistor_3_node;
  wire [3:0] control_unit_1_alu_op_out;
  wire [4:0] control_unit_1_reg_read_a_selector_out, control_unit_1_reg_read_b_selector_out,
       control_unit_1_reg_write_selector_out;
  wire [21:0] demultiplexer_1_out2, demultiplexer_1_out3;
  wire [23:0] adder_1_out, control_unit_1_mem_addr_out, control_unit_1_pc_data_out, multiplexer_1_out,
       multiplexer_2_out, multiplexer_3_out, PC_q;
  wire [23:2] pull_resistor_1_node;
  wire [31:0] alu_1_acc_out, alu_1_aux_out, alu_1_flags_out, AUX_q, control_unit_1_mem_data_out,
       control_unit_1_operand_1, control_unit_1_operand_2, control_unit_1_reg_write_data_out,
       demultiplexer_2_out2, demultiplexer_2_out3, FLAGS_q, IR_q, multiplexer_4_out,
       register_page_1_reg_read_out_a, register_page_1_reg_read_out_b;

  Pull_Resistor #(.pull(1)) pull_resistor_1 (.node(pull_resistor_1_node[2]));
  Adder #(.width(24)) adder_1 (
    .a(PC_q), .b({{21{pull_resistor_1_node[23]}}, pull_resistor_1_node[2], {2{pull_resistor_1_node[23]}}}),
    .out(adder_1_out));  // open: cin, cout
  Pull_Resistor pull_resistor_2 (.node(pull_resistor_1_node[23]));
  Multiplexer #(.width(24)) multiplexer_1 (
    .in0(adder_1_out), .in1(control_unit_1_pc_data_out), .out(multiplexer_1_out),
    .sel(control_unit_1_pc_write_enable));
  or or_1 (or_1_out, control_unit_1_next_instruction_trigger, control_unit_1_pc_write_enable);
  Register #(.width(24)) PC (.D(multiplexer_1_out), .en(or_1_out), .clk(CLK), .Q(PC_q));  // open: clr
  Register_Page register_page_1 (
    .REG_WRITE_DATA_IN(control_unit_1_reg_write_data_out),
    .REG_WRITE_SELECTOR(control_unit_1_reg_write_selector_out),
    .REG_READ_SELECTOR_A(control_unit_1_reg_read_a_selector_out),
    .REG_READ_SELECTOR_B(control_unit_1_reg_read_b_selector_out), .CLK_IN(CLK),
    .REG_WRITE_ENABLE(control_unit_1_reg_write_enable_out), .REG_READ_OUT_A(register_page_1_reg_read_out_a),
    .REG_READ_OUT_B(register_page_1_reg_read_out_b));
  or or_2 (or_2_out, and_1_out, and_2_out);
  and and_1 (and_1_out, control_unit_1_alu_op_out[0], control_unit_1_alu_op_out[1], not_1_out, not_2_out);
  not not_1 (not_1_out, control_unit_1_alu_op_out[2]);
  not not_2 (not_2_out, control_unit_1_alu_op_out[3]);
  not not_3 (not_3_out, control_unit_1_alu_op_out[0]);
  and and_2 (and_2_out, not_3_out, control_unit_1_alu_op_out[1], not_4_out, not_5_out);
  not not_4 (not_4_out, control_unit_1_alu_op_out[2]);
  not not_5 (not_5_out, control_unit_1_alu_op_out[3]);
  Register #(.width(32)) IR (
    .D(multiplexer_4_out), .en(control_unit_1_next_instruction_trigger), .clk(CLK), .Q(IR_q),
    .clr(Power_button));
  not not_6 (not_6_out, control_unit_1_bootstrap_state);
  Pull_Resistor pull_resistor_3 (.node(pull_resistor_3_node[1]));
  and and_3 (and_3_out, or_2_out, control_unit_1_alu_enable);
  Register #(.width(32)) FLAGS (
    .D(alu_1_flags_out), .en(control_unit_1_alu_enable), .clk(CLK), .Q(FLAGS_q));  // open: clr
  Pull_Resistor #(.pull(1)) pull_resistor_4 (.node(pull_resistor_4_node));
  Counter #(.max('h3), .width(2)) counter_1 (
    .load(control_unit_1_next_instruction_trigger), .D({2{pull_resistor_3_node[1]}}), .count(not_6_out),
    .Q(counter_1_q), .up(pull_resistor_4_node), .clk(CLK));  // open: carry, clr
  Register #(.width(32)) AUX (.D(alu_1_aux_out), .en(and_3_out), .clk(CLK), .Q(AUX_q));  // open: clr
  Control_Unit control_unit_1 (
    .IR_INPUT(IR_q), .CYCLE_COUNT_IN(counter_1_q), .REG_OP_1_IN(register_page_1_reg_read_out_a),
    .REG_OP_2_IN(register_page_1_reg_read_out_b), .MDR_IN(multiplexer_4_out), .ALU_RESULT_IN(alu_1_acc_out),
    .AUX_IN(AUX_q), .FLAGS_IN(FLAGS_q), .PC_IN(PC_q), .CLK_IN(CLK), .Power_Button_In(Power_button),
    .ALU_OP_OUT(control_unit_1_alu_op_out), .OPERAND_1(control_unit_1_operand_1),
    .REG_WRITE_SELECTOR_OUT(control_unit_1_reg_write_selector_out),
    .REG_READ_A_SELECTOR_OUT(control_unit_1_reg_read_a_selector_out),
    .REG_READ_B_SELECTOR_OUT(control_unit_1_reg_read_b_selector_out), .MEM_WRITE_ENABLE(MEM_WRITE_ENABLE),
    .REG_WRITE_ENABLE_OUT(control_unit_1_reg_write_enable_out), .ALU_ENABLE(control_unit_1_alu_enable),
    .MEM_ADDR_EMIT(control_unit_1_mem_addr_emit), .OPERAND_2(control_unit_1_operand_2),
    .MEM_DATA_OUT(control_unit_1_mem_data_out), .QUADBYTE(QUADBYTE),
    .REG_WRITE_DATA_OUT(control_unit_1_reg_write_data_out), .PC_WRITE_ENABLE(control_unit_1_pc_write_enable),
    .NEXT_INSTRUCTION_TRIGGER(control_unit_1_next_instruction_trigger),
    .PC_DATA_OUT(control_unit_1_pc_data_out), .MEM_ADDR_OUT(control_unit_1_mem_addr_out),
    .BOOTSTRAP_STATE(control_unit_1_bootstrap_state));
  ALU alu_1 (
    .REG_B(control_unit_1_operand_2), .REG_A(control_unit_1_operand_1),
    .OPCODE_SELECTOR(control_unit_1_alu_op_out), .ACC_OUT(alu_1_acc_out), .AUX_OUT(alu_1_aux_out),
    .FLAGS_OUT(alu_1_flags_out));
  buf buffer_1 (buffer_1_out, control_unit_1_mem_addr_emit);
  Pull_Resistor pull_resistor_5 (.node(buffer_1_out));
  buf buffer_2 (buffer_1_out, control_unit_1_next_instruction_trigger);
  Multiplexer #(.width(24)) multiplexer_2 (
    .in0({24{1'b0}}), .in1(control_unit_1_mem_addr_out), .out(multiplexer_2_out), .sel(buffer_1_out));
  Multiplexer #(.width(24)) multiplexer_3 (
    .in0(multiplexer_2_out), .in1(PC_q),
    .out({multiplexer_3_out[23], MEM_ADDR_OUT[22], multiplexer_3_out[21:0]}),
    .sel(control_unit_1_next_instruction_trigger));
  Demultiplexer #(.select(2), .width(22)) demultiplexer_1 (
    .out0(BOOT_ROM_ADDR), .out1(PERIPH_ADDR_OUT), .out2(demultiplexer_1_out2), .out3(demultiplexer_1_out3),
    .in(multiplexer_3_out[21:0]), .sel({multiplexer_3_out[23], MEM_ADDR_OUT[22]}));
  assign MEM_ADDR_OUT[21:0] = demultiplexer_1_out2 | demultiplexer_1_out3;  // OR_Gate or_3, 22 bits wide
  Multiplexer #(.select(2), .width(32)) multiplexer_4 (
    .in0(BOOT_ROM_DATA), .in1(PERIPH_DATA_IN), .in2(MEM_DATA_IN), .in3(MEM_DATA_IN), .out(multiplexer_4_out),
    .sel({multiplexer_3_out[23], MEM_ADDR_OUT[22]}));
  Demultiplexer #(.select(2), .width(32)) demultiplexer_2 (
    .out1(PERIPH_DATA_OUT), .out2(demultiplexer_2_out2), .out3(demultiplexer_2_out3),
    .in(control_unit_1_mem_data_out), .sel({multiplexer_3_out[23], MEM_ADDR_OUT[22]}));  // open: out0
  assign MEM_DATA_OUT = demultiplexer_2_out2 | demultiplexer_2_out3;  // OR_Gate or_4, 32 bits wide

  // Notes on the sheet:
  //   Multiply or divide
  //   buffer_1 drives only 1 and floats otherwise
  //   buffer_2 drives only 1 and floats otherwise
endmodule

module OR_32 (
  input  [31:0] in_1,
  input  [31:0] in_2,
  output [31:0] out_3
);

  buf or_1 (out_3[0], in_2[0]);  // OR_Gate
  buf or_2 (out_3[1], in_2[1]);  // OR_Gate
  buf or_3 (out_3[2], in_2[2]);  // OR_Gate
  buf or_4 (out_3[3], in_2[3]);  // OR_Gate
  buf or_5 (out_3[4], in_2[4]);  // OR_Gate
  buf or_6 (out_3[5], in_2[5]);  // OR_Gate
  buf or_7 (out_3[6], in_2[6]);  // OR_Gate
  buf or_8 (out_3[7], in_2[7]);  // OR_Gate
  buf or_9 (out_3[8], in_2[8]);  // OR_Gate
  buf or_10 (out_3[9], in_2[9]);  // OR_Gate
  buf or_11 (out_3[10], in_2[10]);  // OR_Gate
  buf or_12 (out_3[11], in_2[11]);  // OR_Gate
  buf or_13 (out_3[12], in_2[12]);  // OR_Gate
  buf or_14 (out_3[13], in_2[13]);  // OR_Gate
  buf or_15 (out_3[14], in_2[14]);  // OR_Gate
  buf or_16 (out_3[15], in_2[15]);  // OR_Gate
  buf or_17 (out_3[16], in_2[16]);  // OR_Gate
  buf or_18 (out_3[17], in_2[17]);  // OR_Gate
  buf or_19 (out_3[18], in_2[18]);  // OR_Gate
  // OR_Gate or_20 has open pins: in1=in_2[18], out=open
  or or_21 (out_3[19], in_1[19], in_2[19]);
  or or_22 (out_3[20], in_1[20], in_2[20]);
  or or_23 (out_3[21], in_1[21], in_2[21]);
  or or_24 (out_3[22], in_1[22], in_2[22]);
  or or_25 (out_3[23], in_1[23], in_2[23]);
  or or_26 (out_3[24], in_1[24], in_2[24]);
  or or_27 (out_3[25], in_1[25], in_2[25]);
  or or_28 (out_3[26], in_1[26], in_2[26]);
  or or_29 (out_3[27], in_1[27], in_2[27]);
  or or_30 (out_3[28], in_1[28], in_2[28]);
  or or_31 (out_3[29], in_1[29], in_2[29]);
  or or_32 (out_3[30], in_1[30], in_2[30]);
  or or_33 (out_3[31], in_1[31], in_2[31]);
endmodule

module AND_32 (
  input  [31:0] Input_bus_1,
  input  [31:0] Input_bus_2,
  output [31:0] ACC_OUT
);

  buf and_1 (ACC_OUT[0], Input_bus_2[0]);  // AND_Gate
  buf and_2 (ACC_OUT[1], Input_bus_2[1]);  // AND_Gate
  buf and_3 (ACC_OUT[2], Input_bus_2[2]);  // AND_Gate
  buf and_4 (ACC_OUT[3], Input_bus_2[3]);  // AND_Gate
  buf and_5 (ACC_OUT[4], Input_bus_2[4]);  // AND_Gate
  buf and_6 (ACC_OUT[5], Input_bus_2[5]);  // AND_Gate
  buf and_7 (ACC_OUT[6], Input_bus_2[6]);  // AND_Gate
  buf and_8 (ACC_OUT[7], Input_bus_2[7]);  // AND_Gate
  buf and_9 (ACC_OUT[8], Input_bus_2[8]);  // AND_Gate
  buf and_10 (ACC_OUT[9], Input_bus_2[9]);  // AND_Gate
  buf and_11 (ACC_OUT[10], Input_bus_2[10]);  // AND_Gate
  buf and_12 (ACC_OUT[11], Input_bus_2[11]);  // AND_Gate
  buf and_13 (ACC_OUT[12], Input_bus_2[12]);  // AND_Gate
  buf and_14 (ACC_OUT[13], Input_bus_2[13]);  // AND_Gate
  buf and_15 (ACC_OUT[14], Input_bus_2[14]);  // AND_Gate
  buf and_16 (ACC_OUT[15], Input_bus_2[15]);  // AND_Gate
  buf and_17 (ACC_OUT[16], Input_bus_2[16]);  // AND_Gate
  buf and_18 (ACC_OUT[17], Input_bus_2[17]);  // AND_Gate
  buf and_19 (ACC_OUT[18], Input_bus_2[18]);  // AND_Gate
  buf and_20 (ACC_OUT[19], Input_bus_1[19]);  // AND_Gate
  buf and_21 (ACC_OUT[20], Input_bus_2[20]);  // AND_Gate
  buf and_22 (ACC_OUT[21], Input_bus_2[21]);  // AND_Gate
  buf and_23 (ACC_OUT[22], Input_bus_2[22]);  // AND_Gate
  buf and_24 (ACC_OUT[23], Input_bus_2[23]);  // AND_Gate
  buf and_25 (ACC_OUT[24], Input_bus_2[24]);  // AND_Gate
  buf and_26 (ACC_OUT[25], Input_bus_2[25]);  // AND_Gate
  buf and_27 (ACC_OUT[26], Input_bus_2[26]);  // AND_Gate
  buf and_28 (ACC_OUT[27], Input_bus_2[27]);  // AND_Gate
  buf and_29 (ACC_OUT[28], Input_bus_2[28]);  // AND_Gate
  buf and_30 (ACC_OUT[29], Input_bus_2[29]);  // AND_Gate
  buf and_31 (ACC_OUT[30], Input_bus_2[30]);  // AND_Gate
  buf and_32 (ACC_OUT[31], Input_bus_2[31]);  // AND_Gate
endmodule

module XOR_32 (
  input  [31:0] in_1,
  input  [31:0] in_2,
  output [31:0] out_3
);

  wire and_1_out, and_2_out, and_3_out, and_4_out, and_5_out, and_6_out, and_7_out, and_8_out, and_9_out,
       and_10_out, and_11_out, and_12_out, and_13_out, and_14_out, and_15_out, and_16_out, and_17_out,
       and_18_out, and_19_out, and_20_out, and_21_out, and_22_out, and_23_out, and_24_out, and_25_out,
       and_26_out, and_27_out, and_28_out, and_29_out, and_30_out, and_31_out, and_32_out, nor_1_out,
       nor_2_out, nor_3_out, nor_4_out, nor_5_out, nor_6_out, nor_7_out, nor_8_out, nor_9_out, nor_10_out,
       nor_11_out, nor_12_out, nor_13_out, nor_14_out, nor_15_out, nor_16_out, nor_17_out, nor_18_out,
       nor_19_out, nor_20_out, nor_21_out, nor_22_out, nor_23_out, nor_24_out, nor_25_out, nor_26_out,
       nor_27_out, nor_28_out, nor_29_out, nor_30_out, nor_31_out, nor_32_out, undriven;

  not nor_1 (nor_1_out, in_2[0]);  // NOR_Gate
  not nor_2 (nor_2_out, in_2[1]);  // NOR_Gate
  not nor_3 (nor_3_out, in_2[2]);  // NOR_Gate
  not nor_4 (nor_4_out, in_2[3]);  // NOR_Gate
  not nor_5 (nor_5_out, in_2[4]);  // NOR_Gate
  not nor_6 (nor_6_out, in_2[5]);  // NOR_Gate
  not nor_7 (nor_7_out, in_2[6]);  // NOR_Gate
  not nor_8 (nor_8_out, in_2[7]);  // NOR_Gate
  not nor_9 (nor_9_out, in_2[8]);  // NOR_Gate
  not nor_10 (nor_10_out, in_2[9]);  // NOR_Gate
  not nor_11 (nor_11_out, in_2[10]);  // NOR_Gate
  not nor_12 (nor_12_out, in_2[11]);  // NOR_Gate
  not nor_13 (nor_13_out, in_2[12]);  // NOR_Gate
  not nor_14 (nor_14_out, in_2[13]);  // NOR_Gate
  not nor_15 (nor_15_out, in_2[14]);  // NOR_Gate
  not nor_16 (nor_16_out, in_2[15]);  // NOR_Gate
  not nor_17 (nor_17_out, in_2[16]);  // NOR_Gate
  not nor_18 (nor_18_out, in_2[17]);  // NOR_Gate
  not nor_19 (nor_19_out, in_2[18]);  // NOR_Gate
  not nor_20 (nor_20_out, in_2[19]);  // NOR_Gate
  not nor_21 (nor_21_out, in_2[20]);  // NOR_Gate
  not nor_22 (nor_22_out, in_2[21]);  // NOR_Gate
  not nor_23 (nor_23_out, in_2[22]);  // NOR_Gate
  not nor_24 (nor_24_out, in_2[23]);  // NOR_Gate
  not nor_25 (nor_25_out, in_2[24]);  // NOR_Gate
  not nor_26 (nor_26_out, in_2[25]);  // NOR_Gate
  not nor_27 (nor_27_out, in_2[26]);  // NOR_Gate
  not nor_28 (nor_28_out, in_2[27]);  // NOR_Gate
  not nor_29 (nor_29_out, in_2[28]);  // NOR_Gate
  not nor_30 (nor_30_out, in_2[29]);  // NOR_Gate
  nor nor_31 (nor_31_out, in_1[30], undriven);
  nor nor_32 (nor_32_out, in_1[31], in_2[31]);
  nor nor_33 (out_3[0], nor_1_out, and_1_out);
  // AND_Gate and_1 has open pins: out=and_1_out
  nor nor_34 (out_3[1], nor_2_out, and_2_out);
  // AND_Gate and_2 has open pins: out=and_2_out
  nor nor_35 (out_3[2], nor_3_out, and_3_out);
  // AND_Gate and_3 has open pins: out=and_3_out
  nor nor_36 (out_3[3], nor_4_out, and_4_out);
  // AND_Gate and_4 has open pins: out=and_4_out
  nor nor_37 (out_3[4], nor_5_out, and_5_out);
  // AND_Gate and_5 has open pins: out=and_5_out
  nor nor_38 (out_3[5], nor_6_out, and_6_out);
  // AND_Gate and_6 has open pins: out=and_6_out
  nor nor_39 (out_3[6], nor_7_out, and_7_out);
  // AND_Gate and_7 has open pins: out=and_7_out
  nor nor_40 (out_3[7], nor_8_out, and_8_out);
  // AND_Gate and_8 has open pins: out=and_8_out
  nor nor_41 (out_3[8], nor_9_out, and_9_out);
  // AND_Gate and_9 has open pins: out=and_9_out
  nor nor_42 (out_3[9], nor_10_out, and_10_out);
  // AND_Gate and_10 has open pins: out=and_10_out
  nor nor_43 (out_3[10], nor_11_out, and_11_out);
  // AND_Gate and_11 has open pins: out=and_11_out
  nor nor_44 (out_3[11], nor_12_out, and_12_out);
  // AND_Gate and_12 has open pins: out=and_12_out
  nor nor_45 (out_3[12], nor_13_out, and_13_out);
  // AND_Gate and_13 has open pins: out=and_13_out
  nor nor_46 (out_3[13], nor_14_out, and_14_out);
  // AND_Gate and_14 has open pins: out=and_14_out
  nor nor_47 (out_3[14], nor_15_out, and_15_out);
  // AND_Gate and_15 has open pins: out=and_15_out
  nor nor_48 (out_3[15], nor_16_out, and_16_out);
  // AND_Gate and_16 has open pins: out=and_16_out
  nor nor_49 (out_3[16], nor_17_out, and_17_out);
  // AND_Gate and_17 has open pins: out=and_17_out
  nor nor_50 (out_3[17], nor_18_out, and_18_out);
  // AND_Gate and_18 has open pins: out=and_18_out
  nor nor_51 (out_3[18], nor_19_out, and_19_out);
  // AND_Gate and_19 has open pins: out=and_19_out
  nor nor_52 (out_3[19], nor_20_out, and_20_out);
  // AND_Gate and_20 has open pins: out=and_20_out
  nor nor_53 (out_3[20], nor_21_out, and_21_out);
  // AND_Gate and_21 has open pins: out=and_21_out
  nor nor_54 (out_3[21], nor_22_out, and_22_out);
  // AND_Gate and_22 has open pins: out=and_22_out
  nor nor_55 (out_3[22], nor_23_out, and_23_out);
  // AND_Gate and_23 has open pins: out=and_23_out
  nor nor_56 (out_3[23], nor_24_out, and_24_out);
  // AND_Gate and_24 has open pins: out=and_24_out
  nor nor_57 (out_3[24], nor_25_out, and_25_out);
  // AND_Gate and_25 has open pins: out=and_25_out
  nor nor_58 (out_3[25], nor_26_out, and_26_out);
  // AND_Gate and_26 has open pins: out=and_26_out
  nor nor_59 (out_3[26], nor_27_out, and_27_out);
  // AND_Gate and_27 has open pins: out=and_27_out
  nor nor_60 (out_3[27], nor_28_out, and_28_out);
  // AND_Gate and_28 has open pins: out=and_28_out
  nor nor_61 (out_3[28], nor_29_out, and_29_out);
  // AND_Gate and_29 has open pins: out=and_29_out
  nor nor_62 (out_3[29], nor_30_out, and_30_out);
  // AND_Gate and_30 has open pins: out=and_30_out
  nor nor_63 (out_3[30], nor_31_out, and_31_out);
  and and_31 (and_31_out, in_1[30], in_2[30]);
  nor nor_64 (out_3[31], nor_32_out, and_32_out);
  and and_32 (and_32_out, in_1[31], in_2[31]);
endmodule

module L_1_bit_full_adder_dd117225 (
  input  Input_1,
  input  Input_2,
  input  Carry_In,
  output Output_1,
  output Carry_out
);

  wire and_1_out, and_2_out, xor_1_out;

  xor xor_1 (xor_1_out, Input_1, Input_2);
  xor xor_2 (Output_1, xor_1_out, Carry_In);
  and and_1 (and_1_out, xor_1_out, Carry_In);
  and and_2 (and_2_out, Input_1, Input_2);
  or or_1 (Carry_out, and_1_out, and_2_out);

  // Notes on the sheet:
  //   Sum
  //   Carry
endmodule

module ADD_32 (
  input  [31:0] Input_bus_1,
  input  [31:0] Input_bus_2,
  input  ADD_SUB_CONTROL,
  output [31:0] Output_bus_1,
  output Output_1
);

  wire L_1_bit_full_adder_dd117225_1_carry_out, L_1_bit_full_adder_dd117225_2_carry_out,
       L_1_bit_full_adder_dd117225_3_carry_out, L_1_bit_full_adder_dd117225_4_carry_out,
       L_1_bit_full_adder_dd117225_5_carry_out, L_1_bit_full_adder_dd117225_6_carry_out,
       L_1_bit_full_adder_dd117225_7_carry_out, L_1_bit_full_adder_dd117225_8_carry_out,
       L_1_bit_full_adder_dd117225_9_carry_out, L_1_bit_full_adder_dd117225_10_carry_out,
       L_1_bit_full_adder_dd117225_11_carry_out, L_1_bit_full_adder_dd117225_12_carry_out,
       L_1_bit_full_adder_dd117225_13_carry_out, L_1_bit_full_adder_dd117225_14_carry_out,
       L_1_bit_full_adder_dd117225_15_carry_out, L_1_bit_full_adder_dd117225_16_carry_out,
       L_1_bit_full_adder_dd117225_17_carry_out, L_1_bit_full_adder_dd117225_18_carry_out,
       L_1_bit_full_adder_dd117225_19_carry_out, L_1_bit_full_adder_dd117225_20_carry_out,
       L_1_bit_full_adder_dd117225_21_carry_out, L_1_bit_full_adder_dd117225_22_carry_out,
       L_1_bit_full_adder_dd117225_23_carry_out, L_1_bit_full_adder_dd117225_24_carry_out,
       L_1_bit_full_adder_dd117225_25_carry_out, L_1_bit_full_adder_dd117225_26_carry_out,
       L_1_bit_full_adder_dd117225_27_carry_out, L_1_bit_full_adder_dd117225_28_carry_out,
       L_1_bit_full_adder_dd117225_29_carry_out, L_1_bit_full_adder_dd117225_30_carry_out,
       L_1_bit_full_adder_dd117225_31_carry_out, L_1_bit_full_adder_dd117225_32_carry_out, multiplexer_1_out,
       multiplexer_2_out, multiplexer_3_out, multiplexer_4_out, multiplexer_5_out, multiplexer_6_out,
       multiplexer_7_out, multiplexer_8_out, multiplexer_9_out, multiplexer_10_out, multiplexer_11_out,
       multiplexer_12_out, multiplexer_13_out, multiplexer_14_out, multiplexer_15_out, multiplexer_16_out,
       multiplexer_17_out, multiplexer_18_out, multiplexer_19_out, multiplexer_20_out, multiplexer_21_out,
       multiplexer_22_out, multiplexer_23_out, multiplexer_24_out, multiplexer_25_out, multiplexer_26_out,
       multiplexer_27_out, multiplexer_28_out, multiplexer_29_out, multiplexer_30_out, multiplexer_31_out,
       multiplexer_32_out, not_1_out, not_2_out, not_3_out, not_4_out, not_5_out, not_6_out, not_7_out,
       not_8_out, not_9_out, not_10_out, not_11_out, not_12_out, not_13_out, not_14_out, not_15_out,
       not_16_out, not_17_out, not_18_out, not_19_out, not_20_out, not_21_out, not_22_out, not_23_out,
       not_24_out, not_25_out, not_26_out, not_27_out, not_28_out, not_29_out, not_30_out, not_31_out,
       not_32_out;

  Multiplexer multiplexer_1 (.in0(Input_bus_2[0]), .in1(not_1_out), .out(multiplexer_1_out), .sel(ADD_SUB_CONTROL));
  not not_1 (not_1_out, Input_bus_2[0]);
  Multiplexer multiplexer_2 (.in0(Input_bus_2[1]), .in1(not_2_out), .out(multiplexer_2_out), .sel(ADD_SUB_CONTROL));
  not not_2 (not_2_out, Input_bus_2[1]);
  Multiplexer multiplexer_3 (.in0(Input_bus_2[2]), .in1(not_3_out), .out(multiplexer_3_out), .sel(ADD_SUB_CONTROL));
  not not_3 (not_3_out, Input_bus_2[2]);
  Multiplexer multiplexer_4 (.in0(Input_bus_2[3]), .in1(not_4_out), .out(multiplexer_4_out), .sel(ADD_SUB_CONTROL));
  not not_4 (not_4_out, Input_bus_2[3]);
  Multiplexer multiplexer_5 (.in0(Input_bus_2[4]), .in1(not_5_out), .out(multiplexer_5_out), .sel(ADD_SUB_CONTROL));
  not not_5 (not_5_out, Input_bus_2[4]);
  Multiplexer multiplexer_6 (.in0(Input_bus_2[5]), .in1(not_6_out), .out(multiplexer_6_out), .sel(ADD_SUB_CONTROL));
  not not_6 (not_6_out, Input_bus_2[5]);
  Multiplexer multiplexer_7 (.in0(Input_bus_2[6]), .in1(not_7_out), .out(multiplexer_7_out), .sel(ADD_SUB_CONTROL));
  not not_7 (not_7_out, Input_bus_2[6]);
  Multiplexer multiplexer_8 (.in0(Input_bus_2[7]), .in1(not_8_out), .out(multiplexer_8_out), .sel(ADD_SUB_CONTROL));
  not not_8 (not_8_out, Input_bus_2[7]);
  Multiplexer multiplexer_9 (.in0(Input_bus_2[8]), .in1(not_9_out), .out(multiplexer_9_out), .sel(ADD_SUB_CONTROL));
  not not_9 (not_9_out, Input_bus_2[8]);
  Multiplexer multiplexer_10 (.in0(Input_bus_2[9]), .in1(not_10_out), .out(multiplexer_10_out), .sel(ADD_SUB_CONTROL));
  not not_10 (not_10_out, Input_bus_2[9]);
  Multiplexer multiplexer_11 (.in0(Input_bus_2[10]), .in1(not_11_out), .out(multiplexer_11_out), .sel(ADD_SUB_CONTROL));
  not not_11 (not_11_out, Input_bus_2[10]);
  Multiplexer multiplexer_12 (.in0(Input_bus_2[11]), .in1(not_12_out), .out(multiplexer_12_out), .sel(ADD_SUB_CONTROL));
  not not_12 (not_12_out, Input_bus_2[11]);
  Multiplexer multiplexer_13 (.in0(Input_bus_2[12]), .in1(not_13_out), .out(multiplexer_13_out), .sel(ADD_SUB_CONTROL));
  not not_13 (not_13_out, Input_bus_2[12]);
  Multiplexer multiplexer_14 (.in0(Input_bus_2[13]), .in1(not_14_out), .out(multiplexer_14_out), .sel(ADD_SUB_CONTROL));
  not not_14 (not_14_out, Input_bus_2[13]);
  Multiplexer multiplexer_15 (.in0(Input_bus_2[14]), .in1(not_15_out), .out(multiplexer_15_out), .sel(ADD_SUB_CONTROL));
  not not_15 (not_15_out, Input_bus_2[14]);
  Multiplexer multiplexer_16 (.in0(Input_bus_2[15]), .in1(not_16_out), .out(multiplexer_16_out), .sel(ADD_SUB_CONTROL));
  not not_16 (not_16_out, Input_bus_2[15]);
  Multiplexer multiplexer_17 (.in0(Input_bus_2[16]), .in1(not_17_out), .out(multiplexer_17_out), .sel(ADD_SUB_CONTROL));
  not not_17 (not_17_out, Input_bus_2[16]);
  Multiplexer multiplexer_18 (.in0(Input_bus_2[17]), .in1(not_18_out), .out(multiplexer_18_out), .sel(ADD_SUB_CONTROL));
  not not_18 (not_18_out, Input_bus_2[17]);
  Multiplexer multiplexer_19 (.in0(Input_bus_2[18]), .in1(not_19_out), .out(multiplexer_19_out), .sel(ADD_SUB_CONTROL));
  not not_19 (not_19_out, Input_bus_2[18]);
  Multiplexer multiplexer_20 (.in0(Input_bus_2[19]), .in1(not_20_out), .out(multiplexer_20_out), .sel(ADD_SUB_CONTROL));
  not not_20 (not_20_out, Input_bus_2[19]);
  Multiplexer multiplexer_21 (.in0(Input_bus_2[20]), .in1(not_21_out), .out(multiplexer_21_out), .sel(ADD_SUB_CONTROL));
  not not_21 (not_21_out, Input_bus_2[20]);
  Multiplexer multiplexer_22 (.in0(Input_bus_2[21]), .in1(not_22_out), .out(multiplexer_22_out), .sel(ADD_SUB_CONTROL));
  not not_22 (not_22_out, Input_bus_2[21]);
  Multiplexer multiplexer_23 (.in0(Input_bus_2[22]), .in1(not_23_out), .out(multiplexer_23_out), .sel(ADD_SUB_CONTROL));
  not not_23 (not_23_out, Input_bus_2[22]);
  Multiplexer multiplexer_24 (.in0(Input_bus_2[23]), .in1(not_24_out), .out(multiplexer_24_out), .sel(ADD_SUB_CONTROL));
  not not_24 (not_24_out, Input_bus_2[23]);
  Multiplexer multiplexer_25 (.in0(Input_bus_2[24]), .in1(not_25_out), .out(multiplexer_25_out), .sel(ADD_SUB_CONTROL));
  not not_25 (not_25_out, Input_bus_2[24]);
  Multiplexer multiplexer_26 (.in0(Input_bus_2[25]), .in1(not_26_out), .out(multiplexer_26_out), .sel(ADD_SUB_CONTROL));
  not not_26 (not_26_out, Input_bus_2[25]);
  Multiplexer multiplexer_27 (.in0(Input_bus_2[26]), .in1(not_27_out), .out(multiplexer_27_out), .sel(ADD_SUB_CONTROL));
  not not_27 (not_27_out, Input_bus_2[26]);
  Multiplexer multiplexer_28 (.in0(Input_bus_2[27]), .in1(not_28_out), .out(multiplexer_28_out), .sel(ADD_SUB_CONTROL));
  not not_28 (not_28_out, Input_bus_2[27]);
  Multiplexer multiplexer_29 (.in0(Input_bus_2[28]), .in1(not_29_out), .out(multiplexer_29_out), .sel(ADD_SUB_CONTROL));
  not not_29 (not_29_out, Input_bus_2[28]);
  Multiplexer multiplexer_30 (.in0(Input_bus_2[29]), .in1(not_30_out), .out(multiplexer_30_out), .sel(ADD_SUB_CONTROL));
  not not_30 (not_30_out, Input_bus_2[29]);
  Multiplexer multiplexer_31 (.in0(Input_bus_2[30]), .in1(not_31_out), .out(multiplexer_31_out), .sel(ADD_SUB_CONTROL));
  not not_31 (not_31_out, Input_bus_2[30]);
  Multiplexer multiplexer_32 (.in0(Input_bus_2[31]), .in1(not_32_out), .out(multiplexer_32_out), .sel(ADD_SUB_CONTROL));
  not not_32 (not_32_out, Input_bus_2[31]);
  L_1_bit_full_adder_dd117225 L_1_bit_full_adder_dd117225_1 (
    .Input_1(Input_bus_1[0]), .Input_2(multiplexer_1_out), .Carry_In(ADD_SUB_CONTROL),
    .Output_1(Output_bus_1[0]), .Carry_out(L_1_bit_full_adder_dd117225_1_carry_out));
  L_1_bit_full_adder_dd117225 L_1_bit_full_adder_dd117225_2 (
    .Input_1(Input_bus_1[1]), .Input_2(multiplexer_2_out),
    .Carry_In(L_1_bit_full_adder_dd117225_1_carry_out), .Output_1(Output_bus_1[1]),
    .Carry_out(L_1_bit_full_adder_dd117225_2_carry_out));
  L_1_bit_full_adder_dd117225 L_1_bit_full_adder_dd117225_3 (
    .Input_1(Input_bus_1[2]), .Input_2(multiplexer_3_out),
    .Carry_In(L_1_bit_full_adder_dd117225_2_carry_out), .Output_1(Output_bus_1[2]),
    .Carry_out(L_1_bit_full_adder_dd117225_3_carry_out));
  L_1_bit_full_adder_dd117225 L_1_bit_full_adder_dd117225_4 (
    .Input_1(Input_bus_1[3]), .Input_2(multiplexer_4_out),
    .Carry_In(L_1_bit_full_adder_dd117225_3_carry_out), .Output_1(Output_bus_1[3]),
    .Carry_out(L_1_bit_full_adder_dd117225_4_carry_out));
  L_1_bit_full_adder_dd117225 L_1_bit_full_adder_dd117225_5 (
    .Input_1(Input_bus_1[4]), .Input_2(multiplexer_5_out),
    .Carry_In(L_1_bit_full_adder_dd117225_4_carry_out), .Output_1(Output_bus_1[4]),
    .Carry_out(L_1_bit_full_adder_dd117225_5_carry_out));
  L_1_bit_full_adder_dd117225 L_1_bit_full_adder_dd117225_6 (
    .Input_1(Input_bus_1[5]), .Input_2(multiplexer_6_out),
    .Carry_In(L_1_bit_full_adder_dd117225_5_carry_out), .Output_1(Output_bus_1[5]),
    .Carry_out(L_1_bit_full_adder_dd117225_6_carry_out));
  L_1_bit_full_adder_dd117225 L_1_bit_full_adder_dd117225_7 (
    .Input_1(Input_bus_1[6]), .Input_2(multiplexer_7_out),
    .Carry_In(L_1_bit_full_adder_dd117225_6_carry_out), .Output_1(Output_bus_1[6]),
    .Carry_out(L_1_bit_full_adder_dd117225_7_carry_out));
  L_1_bit_full_adder_dd117225 L_1_bit_full_adder_dd117225_8 (
    .Input_1(Input_bus_1[7]), .Input_2(multiplexer_8_out),
    .Carry_In(L_1_bit_full_adder_dd117225_7_carry_out), .Output_1(Output_bus_1[7]),
    .Carry_out(L_1_bit_full_adder_dd117225_8_carry_out));
  L_1_bit_full_adder_dd117225 L_1_bit_full_adder_dd117225_9 (
    .Input_1(Input_bus_1[8]), .Input_2(multiplexer_9_out),
    .Carry_In(L_1_bit_full_adder_dd117225_8_carry_out), .Output_1(Output_bus_1[8]),
    .Carry_out(L_1_bit_full_adder_dd117225_9_carry_out));
  L_1_bit_full_adder_dd117225 L_1_bit_full_adder_dd117225_10 (
    .Input_1(Input_bus_1[9]), .Input_2(multiplexer_10_out),
    .Carry_In(L_1_bit_full_adder_dd117225_9_carry_out), .Output_1(Output_bus_1[9]),
    .Carry_out(L_1_bit_full_adder_dd117225_10_carry_out));
  L_1_bit_full_adder_dd117225 L_1_bit_full_adder_dd117225_11 (
    .Input_1(Input_bus_1[10]), .Input_2(multiplexer_11_out),
    .Carry_In(L_1_bit_full_adder_dd117225_10_carry_out), .Output_1(Output_bus_1[10]),
    .Carry_out(L_1_bit_full_adder_dd117225_11_carry_out));
  L_1_bit_full_adder_dd117225 L_1_bit_full_adder_dd117225_12 (
    .Input_1(Input_bus_1[11]), .Input_2(multiplexer_12_out),
    .Carry_In(L_1_bit_full_adder_dd117225_11_carry_out), .Output_1(Output_bus_1[11]),
    .Carry_out(L_1_bit_full_adder_dd117225_12_carry_out));
  L_1_bit_full_adder_dd117225 L_1_bit_full_adder_dd117225_13 (
    .Input_1(Input_bus_1[12]), .Input_2(multiplexer_13_out),
    .Carry_In(L_1_bit_full_adder_dd117225_12_carry_out), .Output_1(Output_bus_1[12]),
    .Carry_out(L_1_bit_full_adder_dd117225_13_carry_out));
  L_1_bit_full_adder_dd117225 L_1_bit_full_adder_dd117225_14 (
    .Input_1(Input_bus_1[13]), .Input_2(multiplexer_14_out),
    .Carry_In(L_1_bit_full_adder_dd117225_13_carry_out), .Output_1(Output_bus_1[13]),
    .Carry_out(L_1_bit_full_adder_dd117225_14_carry_out));
  L_1_bit_full_adder_dd117225 L_1_bit_full_adder_dd117225_15 (
    .Input_1(Input_bus_1[14]), .Input_2(multiplexer_15_out),
    .Carry_In(L_1_bit_full_adder_dd117225_14_carry_out), .Output_1(Output_bus_1[14]),
    .Carry_out(L_1_bit_full_adder_dd117225_15_carry_out));
  L_1_bit_full_adder_dd117225 L_1_bit_full_adder_dd117225_16 (
    .Input_1(Input_bus_1[15]), .Input_2(multiplexer_16_out),
    .Carry_In(L_1_bit_full_adder_dd117225_15_carry_out), .Output_1(Output_bus_1[15]),
    .Carry_out(L_1_bit_full_adder_dd117225_16_carry_out));
  L_1_bit_full_adder_dd117225 L_1_bit_full_adder_dd117225_17 (
    .Input_1(Input_bus_1[16]), .Input_2(multiplexer_17_out),
    .Carry_In(L_1_bit_full_adder_dd117225_16_carry_out), .Output_1(Output_bus_1[16]),
    .Carry_out(L_1_bit_full_adder_dd117225_17_carry_out));
  L_1_bit_full_adder_dd117225 L_1_bit_full_adder_dd117225_18 (
    .Input_1(Input_bus_1[17]), .Input_2(multiplexer_18_out),
    .Carry_In(L_1_bit_full_adder_dd117225_17_carry_out), .Output_1(Output_bus_1[17]),
    .Carry_out(L_1_bit_full_adder_dd117225_18_carry_out));
  L_1_bit_full_adder_dd117225 L_1_bit_full_adder_dd117225_19 (
    .Input_1(Input_bus_1[18]), .Input_2(multiplexer_19_out),
    .Carry_In(L_1_bit_full_adder_dd117225_18_carry_out), .Output_1(Output_bus_1[18]),
    .Carry_out(L_1_bit_full_adder_dd117225_19_carry_out));
  L_1_bit_full_adder_dd117225 L_1_bit_full_adder_dd117225_20 (
    .Input_1(Input_bus_1[19]), .Input_2(multiplexer_20_out),
    .Carry_In(L_1_bit_full_adder_dd117225_19_carry_out), .Output_1(Output_bus_1[19]),
    .Carry_out(L_1_bit_full_adder_dd117225_20_carry_out));
  L_1_bit_full_adder_dd117225 L_1_bit_full_adder_dd117225_21 (
    .Input_1(Input_bus_1[20]), .Input_2(multiplexer_21_out),
    .Carry_In(L_1_bit_full_adder_dd117225_20_carry_out), .Output_1(Output_bus_1[20]),
    .Carry_out(L_1_bit_full_adder_dd117225_21_carry_out));
  L_1_bit_full_adder_dd117225 L_1_bit_full_adder_dd117225_22 (
    .Input_1(Input_bus_1[21]), .Input_2(multiplexer_22_out),
    .Carry_In(L_1_bit_full_adder_dd117225_21_carry_out), .Output_1(Output_bus_1[21]),
    .Carry_out(L_1_bit_full_adder_dd117225_22_carry_out));
  L_1_bit_full_adder_dd117225 L_1_bit_full_adder_dd117225_23 (
    .Input_1(Input_bus_1[22]), .Input_2(multiplexer_23_out),
    .Carry_In(L_1_bit_full_adder_dd117225_22_carry_out), .Output_1(Output_bus_1[22]),
    .Carry_out(L_1_bit_full_adder_dd117225_23_carry_out));
  L_1_bit_full_adder_dd117225 L_1_bit_full_adder_dd117225_24 (
    .Input_1(Input_bus_1[23]), .Input_2(multiplexer_24_out),
    .Carry_In(L_1_bit_full_adder_dd117225_23_carry_out), .Output_1(Output_bus_1[23]),
    .Carry_out(L_1_bit_full_adder_dd117225_24_carry_out));
  L_1_bit_full_adder_dd117225 L_1_bit_full_adder_dd117225_25 (
    .Input_1(Input_bus_1[24]), .Input_2(multiplexer_25_out),
    .Carry_In(L_1_bit_full_adder_dd117225_24_carry_out), .Output_1(Output_bus_1[24]),
    .Carry_out(L_1_bit_full_adder_dd117225_25_carry_out));
  L_1_bit_full_adder_dd117225 L_1_bit_full_adder_dd117225_26 (
    .Input_1(Input_bus_1[25]), .Input_2(multiplexer_26_out),
    .Carry_In(L_1_bit_full_adder_dd117225_25_carry_out), .Output_1(Output_bus_1[25]),
    .Carry_out(L_1_bit_full_adder_dd117225_26_carry_out));
  L_1_bit_full_adder_dd117225 L_1_bit_full_adder_dd117225_27 (
    .Input_1(Input_bus_1[26]), .Input_2(multiplexer_27_out),
    .Carry_In(L_1_bit_full_adder_dd117225_26_carry_out), .Output_1(Output_bus_1[26]),
    .Carry_out(L_1_bit_full_adder_dd117225_27_carry_out));
  L_1_bit_full_adder_dd117225 L_1_bit_full_adder_dd117225_28 (
    .Input_1(Input_bus_1[27]), .Input_2(multiplexer_28_out),
    .Carry_In(L_1_bit_full_adder_dd117225_27_carry_out), .Output_1(Output_bus_1[27]),
    .Carry_out(L_1_bit_full_adder_dd117225_28_carry_out));
  L_1_bit_full_adder_dd117225 L_1_bit_full_adder_dd117225_29 (
    .Input_1(Input_bus_1[28]), .Input_2(multiplexer_29_out),
    .Carry_In(L_1_bit_full_adder_dd117225_28_carry_out), .Output_1(Output_bus_1[28]),
    .Carry_out(L_1_bit_full_adder_dd117225_29_carry_out));
  L_1_bit_full_adder_dd117225 L_1_bit_full_adder_dd117225_30 (
    .Input_1(Input_bus_1[29]), .Input_2(multiplexer_30_out),
    .Carry_In(L_1_bit_full_adder_dd117225_29_carry_out), .Output_1(Output_bus_1[29]),
    .Carry_out(L_1_bit_full_adder_dd117225_30_carry_out));
  L_1_bit_full_adder_dd117225 L_1_bit_full_adder_dd117225_31 (
    .Input_1(Input_bus_1[30]), .Input_2(multiplexer_31_out),
    .Carry_In(L_1_bit_full_adder_dd117225_30_carry_out), .Output_1(Output_bus_1[30]),
    .Carry_out(L_1_bit_full_adder_dd117225_31_carry_out));
  L_1_bit_full_adder_dd117225 L_1_bit_full_adder_dd117225_32 (
    .Input_1(Input_bus_1[31]), .Input_2(multiplexer_32_out),
    .Carry_In(L_1_bit_full_adder_dd117225_31_carry_out), .Output_1(Output_bus_1[31]),
    .Carry_out(L_1_bit_full_adder_dd117225_32_carry_out));
  xor xor_1 (Output_1, L_1_bit_full_adder_dd117225_32_carry_out, ADD_SUB_CONTROL);

  // Notes on the sheet:
  //   Carry
endmodule

module Control_Unit (
  input  [31:0] FLAGS_IN,
  input  [1:0] CYCLE_COUNT_IN,
  input  [31:0] IR_INPUT,
  input  CLK_IN,
  input  Power_Button_In,
  input  [31:0] REG_OP_1_IN,
  input  [23:0] PC_IN,
  input  [31:0] REG_OP_2_IN,
  input  [31:0] MDR_IN,
  input  [31:0] ALU_RESULT_IN,
  input  [31:0] AUX_IN,
  output QUADBYTE,
  output MEM_WRITE_ENABLE,
  output [3:0] ALU_OP_OUT,
  output PC_WRITE_ENABLE,
  output NEXT_INSTRUCTION_TRIGGER,
  output REG_WRITE_ENABLE_OUT,
  output ALU_ENABLE,
  output MEM_ADDR_EMIT,
  output BOOTSTRAP_STATE,
  output [31:0] OPERAND_1,
  output [31:0] OPERAND_2,
  output [31:0] MEM_DATA_OUT,
  output [4:0] REG_WRITE_SELECTOR_OUT,
  output [4:0] REG_READ_A_SELECTOR_OUT,
  output [4:0] REG_READ_B_SELECTOR_OUT,
  output [31:0] REG_WRITE_DATA_OUT,
  output [23:0] PC_DATA_OUT,
  output [23:0] MEM_ADDR_OUT
);

  wire and_1_out, and_2_out, and_3_out, and_4_out, and_5_out, and_6_out, and_7_out, and_8_out, and_9_out,
       and_10_out, and_11_out, and_12_out, demultiplexer_1_out0, demultiplexer_1_out1, demultiplexer_1_out2,
       demultiplexer_1_out3, demultiplexer_1_out4, demultiplexer_1_out5, demultiplexer_1_out6,
       demultiplexer_1_out7, demultiplexer_1_out8, demultiplexer_1_out9, demultiplexer_1_out10, not_1_out,
       not_2_out, not_3_out, not_4_out, or_1_out, or_2_out, or_4_out, or_6_out, or_7_out,
       pull_resistor_5_node, xor_1_out;
  wire [1:0] pla_1_out_2;
  wire [3:3] pull_resistor_1_node, pull_resistor_2_node;
  wire [11:0] pull_resistor_4_node;
  wire [23:0] adder_1_out, adder_2_out, multiplexer_12_out, multiplexer_15_out, multiplexer_16_out;
  wire [26:0] pla_1_out;
  wire [31:0] multiplexer_4_out, multiplexer_5_out, multiplexer_6_out, multiplexer_7_out, multiplexer_9_out,
       multiplexer_11_out, multiplexer_13_out, not_5_out;
  wire [31:31] pull_resistor_3_node;

  Pull_Resistor pull_resistor_1 (.node(pull_resistor_1_node[3]));
  Pull_Resistor pull_resistor_2 (.node(pull_resistor_2_node[3]));
  Pull_Resistor pull_resistor_3 (.node(pull_resistor_3_node[31]));
  Pull_Resistor pull_resistor_4 (.node(pull_resistor_4_node));
  xor xor_1 (xor_1_out, FLAGS_IN[2], FLAGS_IN[1]);
  or or_1 (or_1_out, xor_1_out, FLAGS_IN[3]);
  and and_1 (and_1_out, FLAGS_IN[3], demultiplexer_1_out10);
  and and_2 (and_2_out, not_1_out, demultiplexer_1_out9);
  PLA #(.in_width(9), .out_width(28), .\table ("000000001 0000000100000000000100000000\n000010000 0010011001010000000100000000\n010010000 1100010000000010001110000001\n100010000 0000000100000000000100000000\n000010001 0010011001010000000100000000\n010010001 1100010000000010011110000001\n100010001 0000000100000000000100000000\n000010010 1000000010000010000100000010\n010010010 0010011000110000000100000000\n100010010 0000000100000000000100000000\n000010011 0010011001010000000100000000\n010010011 1000110000000000001110000000\n100010011 0000000100000000000100000000\n000010100 1000001000001000000100000010\n010010100 0010011000110000000100000000\n100010100 0000000100000000000100000000\n001000000 0001101100010000000100000000\n001000001 0001101100010000000100000000\n001000010 0001101100010000000100000000\n001000011 0001101100010000000100000000\n001000100 0001101100010000000100000000\n001000101 0001101100010000000100000000\n001000110 0001101100010000000100000000\n001000111 0001101100010000000100000000\n001001000 0001101100010000000100000000\n001001001 0001101100010000000100000000\n001010000 0001001100010000000100000000\n001010001 0001001100010000000100000000\n001010010 0001001100010000000100000000\n001010011 0001001100010000000100000000\n001010100 0001001100010000000100000000\n001010101 0001001100010000000100000000\n001010110 0001001100010000000100000000\n001010111 0001001100010000000100000000\n001011000 0001001100010000000100000000\n001011001 0001001100010000000100000000\n001100111 0001100101000000000100000000\n000100000 0000000000000010000010000000\n010100000 0000000100000000000100000000\n000100001 0000000000000010000011010000\n010100001 0000000100000000000100000000\n000100010 0000000000000010000011001000\n010100010 0000000100000000000100000000\n000100011 0000000000000010000011000000\n010100011 0000000100000000000100000000\n000100100 0000000000000010000010111000\n010100100 0000000100000000000100000000\n000100110 0000000000000010000010110000\n010100110 0000000100000000000100000000\n000100101 0000000000000010000010101000\n010100101 0000000100000000000100000000\n000100111 0000000000000010000010100000\n010100111 0000000100000000000100000000\n000101000 0000000000000010000010011000\n010101000 0000000100000000000100000000\n000101001 0000000000000010000010010000\n010101001 0000000100000000000100000000\n000101010 0000000000000010000010001000\n010101010 0000000100000000000100000000\n000110000 0000000000000010010010000000\n010110000 0000000100000000000100000000\n000110001 0000000000000010010011010000\n010110001 0000000100000000000100000000\n000110010 0000000000000010010011001000\n010110010 0000000100000000000100000000\n000110011 0000000000000010010011000000\n010110011 0000000100000000000100000000\n000110100 0000000000000010010010111000\n010110100 0000000100000000000100000000\n000110110 0000000000000010010010110000\n010110110 0000000100000000000100000000\n000110101 0000000000000010010010101000\n010110101 0000000100000000000100000000\n000110111 0000000000000010010010100000\n010110111 0000000100000000000100000000\n000111000 0000000000000010010010011000\n010111000 0000000100000000000100000000\n000111001 0000000000000010010010010000\n010111001 0000000100000000000100000000\n000111010 0000000000000010010010001000\n010111010 0000000100000000000100000000\n001100000 1000001000001000000100000000\n011100000 0000000100000000000100000000\n001100001 1000001000001000000000000000\n011100001 0000000100000000000100000000\n001100010 1000000000000000001100000000\n011100010 0000000100000000000100000000\n001100011 1000000000000000001000000000\n011100011 0000000100000000000100000000\n001100100 0000001000000001100000000000\n011100100 0000001100000000100100000000\n001100101 0000001000000001100000000000\n011100101 0000001100000100100100000000\n001100110 0000001100000001000100000000\n001101000 0000101100000000000100000000\n001101001 0000001100011000000100000000")) pla_1 (
    .in({CYCLE_COUNT_IN, IR_INPUT[6:0]}),
    .out({MEM_ADDR_EMIT, pla_1_out[26:25], ALU_ENABLE, pla_1_out[23:22], REG_WRITE_ENABLE_OUT, pla_1_out[20:19], pla_1_out_2[0], pla_1_out_2[1], pla_1_out[16:10], MEM_WRITE_ENABLE, pla_1_out[8:0]}));
  Multiplexer #(.select(2), .width(4)) multiplexer_1 (
    .in0(IR_INPUT[3:0]), .in1({{3{pull_resistor_1_node[3]}}, 1'b1}), .in2({4{pull_resistor_2_node[3]}}),
    .out(ALU_OP_OUT), .sel(pla_1_out_2));  // open: in3
  Multiplexer #(.width(5)) multiplexer_2 (
    .in0(IR_INPUT[11:7]), .in1(5'b11101), .out(REG_READ_A_SELECTOR_OUT), .sel(pla_1_out[22]));
  Multiplexer #(.width(5)) multiplexer_3 (
    .in0(IR_INPUT[16:12]), .in1(5'b11101), .out(REG_READ_B_SELECTOR_OUT), .sel(pla_1_out[1]));
  not not_1 (not_1_out, FLAGS_IN[3]);
  and and_3 (and_3_out, or_1_out, demultiplexer_1_out8);
  and and_4 (and_4_out, xor_1_out, demultiplexer_1_out7);
  or or_2 (or_2_out, demultiplexer_1_out0, and_1_out, and_2_out, and_3_out, and_4_out, and_5_out, and_6_out, and_9_out, and_10_out, and_11_out, and_12_out);
  Multiplexer #(.width(32)) multiplexer_4 (.in0(32'h1), .in1(32'h4), .out(multiplexer_4_out), .sel(pla_1_out[8]));
  Multiplexer #(.width(32)) multiplexer_5 (
    .in0({{12{pull_resistor_3_node[31]}}, IR_INPUT[31:12]}), .in1(multiplexer_4_out),
    .out(multiplexer_5_out), .sel(pla_1_out[25]));
  Multiplexer #(.width(32)) multiplexer_6 (
    .in0({IR_INPUT[31:12], pull_resistor_4_node}), .in1({pull_resistor_4_node, IR_INPUT[31:12]}),
    .out(multiplexer_6_out), .sel(pla_1_out[14]));
  Multiplexer #(.width(32)) multiplexer_7 (
    .in0(REG_OP_2_IN), .in1(REG_OP_1_IN), .out(multiplexer_7_out), .sel(pla_1_out[7]));
  and and_5 (and_5_out, and_7_out, demultiplexer_1_out6);
  and and_6 (and_6_out, not_3_out, demultiplexer_1_out5);
  not not_2 (not_2_out, FLAGS_IN[3]);
  not not_3 (not_3_out, xor_1_out);
  and and_7 (and_7_out, not_3_out, not_2_out);
  Multiplexer #(.width(32)) multiplexer_8 (
    .in0(multiplexer_5_out), .in1(REG_OP_2_IN), .out(OPERAND_2), .sel(pla_1_out[23]));
  Multiplexer #(.width(32)) multiplexer_9 (
    .in0(REG_OP_1_IN), .in1(REG_OP_2_IN), .out(multiplexer_9_out), .sel(pla_1_out[23]));
  Multiplexer #(.width(32)) multiplexer_10 (
    .in0(multiplexer_9_out), .in1({{8{1'b0}}, PC_IN}), .out(MEM_DATA_OUT), .sel(pla_1_out[26]));
  Multiplexer #(.select(2), .width(32)) multiplexer_11 (
    .in0(REG_OP_2_IN), .in1(MDR_IN), .in2(ALU_RESULT_IN), .in3(AUX_IN), .out(multiplexer_11_out),
    .sel(pla_1_out[16:15]));
  Multiplexer #(.width(24)) multiplexer_12 (
    .in0({{10{IR_INPUT[31]}}, IR_INPUT[30:17]}), .in1({{9{IR_INPUT[27]}}, IR_INPUT[26:12]}),
    .out(multiplexer_12_out), .sel(pla_1_out[13]));
  not not_4 (not_4_out, FLAGS_IN[0]);
  and and_8 (and_8_out, not_2_out, not_4_out);
  assign not_5_out = ~REG_OP_1_IN;  // NOT_Gate not_5, 32 bits wide
  Multiplexer #(.select(2), .width(32)) multiplexer_13 (
    .in0(multiplexer_11_out), .in1(multiplexer_6_out), .in2(not_5_out), .in3({32{1'b0}}),
    .out(multiplexer_13_out));  // open: sel
  Adder #(.width(24)) adder_1 (.a(PC_IN), .b(multiplexer_12_out), .out(adder_1_out));  // open: cin, cout
  Adder #(.width(24)) adder_2 (
    .a(multiplexer_7_out[23:0]), .b(multiplexer_12_out), .out(adder_2_out));  // open: cin, cout
  and and_9 (and_9_out, and_8_out, demultiplexer_1_out1);
  or or_3 (QUADBYTE, pla_1_out[8], pla_1_out[20], BOOTSTRAP_STATE);
  Multiplexer #(.width(32)) multiplexer_14 (
    .in0(multiplexer_13_out), .in1({{8{1'b0}}, PC_IN}), .out(REG_WRITE_DATA_OUT), .sel(pla_1_out[26]));
  and and_10 (and_10_out, not_4_out, demultiplexer_1_out2);
  and and_11 (and_11_out, FLAGS_IN[0], demultiplexer_1_out3);
  and and_12 (and_12_out, or_4_out, demultiplexer_1_out4);
  or or_4 (or_4_out, FLAGS_IN[3], FLAGS_IN[0]);
  or or_5 (NEXT_INSTRUCTION_TRIGGER, pla_1_out[20], BOOTSTRAP_STATE);
  Multiplexer #(.width(24)) multiplexer_15 (
    .in0(adder_2_out), .in1(adder_1_out), .out(multiplexer_15_out), .sel(pla_1_out[10]));
  Multiplexer #(.width(24)) multiplexer_16 (
    .in0(multiplexer_15_out), .in1(MDR_IN[23:0]), .out(multiplexer_16_out), .sel(pla_1_out[19]));
  and and_13 (PC_WRITE_ENABLE, or_2_out, pla_1_out[13]);
  or or_6 (or_6_out, CLK_IN, or_7_out);
  or or_7 (or_7_out, Power_Button_In, BOOTSTRAP_STATE);
  Multiplexer #(.width(24)) multiplexer_17 (
    .in0(multiplexer_16_out), .in1(REG_OP_2_IN[23:0]), .out(PC_DATA_OUT), .sel(pla_1_out[2]));
  Multiplexer #(.width(24)) multiplexer_18 (
    .in0(adder_2_out), .in1(multiplexer_7_out[23:0]), .out(MEM_ADDR_OUT), .sel(pla_1_out[0]));
  T_Flip_Flop t_ff_1 (.T(or_6_out), .clk(CLK_IN), .Q(BOOTSTRAP_STATE));  // open: Qn, reset, preset
  Pull_Resistor #(.pull(1)) pull_resistor_5 (.node(pull_resistor_5_node));
  Demultiplexer #(.select(4)) demultiplexer_1 (
    .out0(demultiplexer_1_out0), .out1(demultiplexer_1_out1), .out2(demultiplexer_1_out2),
    .out3(demultiplexer_1_out3), .out4(demultiplexer_1_out4), .out5(demultiplexer_1_out5),
    .out6(demultiplexer_1_out6), .out7(demultiplexer_1_out7), .out8(demultiplexer_1_out8),
    .out9(demultiplexer_1_out9), .out10(demultiplexer_1_out10), .in(pull_resistor_5_node),
    .sel(pla_1_out[6:3]));  // open: out11, out12, out13, out14, out15

  assign OPERAND_1 = REG_OP_1_IN;
  assign REG_WRITE_SELECTOR_OUT = REG_READ_A_SELECTOR_OUT;

  // Notes on the sheet:
  //   REG_A
  //   REG_B
  //   reg_b_sp
  //   Upper 16
  //   Signed A < B
  //   Signed A <= B
  //   Lower 16
  //   A == B
  //   sub_alu
  //   add_alu
  //   20-bit immediate values
  //   A != B
  //   Signed A >= B
  //   Signed A > B
  //   pc_to_mem
  //   Sign extend 16-bit value to 24-bit
  //   Unsigned A > B
  //   Get 24-bit value from 32-bit register
  //   Unsigned A >= B
  //   Unsigned A < B
  //   Unsigned <=
  //   Only send through if the condition allows for it
  //   mem_to_pc
  //   skip agu (push/pop/call/ret)
endmodule

module ALU (
  input  [3:0] OPCODE_SELECTOR,
  input  [31:0] REG_A,
  input  [31:0] REG_B,
  output [31:0] ACC_OUT,
  output [31:0] AUX_OUT,
  output [31:0] FLAGS_OUT
);

  wire and_1_out, and_2_out, and_3_out, and_4_out, and_5_out, and_7_out, and_8_out, and_10_out, not_1_out,
       not_2_out, not_3_out, not_4_out, not_5_out, not_6_out, not_7_out, not_8_out, not_9_out, or_1_out,
       or_3_out, xor_1_out, xor_2_out;
  wire [29:28] pull_resistor_2_node;
  wire [31:0] add_32_1_output_bus_1, and_6_out, divider_1_out, divider_1_rem, multiplier_1_cout,
       multiplier_1_out, not_10_out, or_2_out, pull_resistor_1_node, shifter_1_out, shifter_2_out,
       shifter_3_out, xor_3_out;

  ADD_32 add_32_1 (
    .Input_bus_2(REG_B), .Input_bus_1(REG_A), .ADD_SUB_CONTROL(OPCODE_SELECTOR[0]),
    .Output_bus_1(add_32_1_output_bus_1), .Output_1(FLAGS_OUT[0]));
  Pull_Resistor pull_resistor_1 (.node(pull_resistor_1_node));
  Multiplier #(.width(32)) multiplier_1 (
    .a(REG_A), .b(REG_B), .out(multiplier_1_out), .cin(pull_resistor_1_node), .cout(multiplier_1_cout));
  not not_1 (not_1_out, OPCODE_SELECTOR[3]);
  not not_2 (not_2_out, OPCODE_SELECTOR[2]);
  not not_3 (not_3_out, OPCODE_SELECTOR[1]);
  and and_1 (and_1_out, not_1_out, not_2_out, not_3_out);
  and and_2 (and_2_out, REG_A[31], REG_B[31]);
  not not_4 (not_4_out, REG_A[31]);
  and and_3 (and_3_out, not_4_out, not_5_out);
  not not_5 (not_5_out, REG_A[31]);
  Divider #(.width(32)) divider_1 (.a(REG_A), .b(REG_B), .out(divider_1_out), .rem(divider_1_rem));  // open: upper
  not not_6 (not_6_out, OPCODE_SELECTOR[0]);
  and and_4 (and_4_out, not_6_out, or_1_out);
  or or_1 (or_1_out, and_2_out, and_3_out);
  and and_5 (and_5_out, OPCODE_SELECTOR[0], xor_1_out);
  xor xor_1 (xor_1_out, REG_A[31], REG_B[31]);
  assign and_6_out = REG_A & REG_B;  // AND_Gate and_6, 32 bits wide
  and and_7 (and_7_out, and_1_out, and_4_out);
  and and_8 (and_8_out, and_1_out, and_5_out);
  assign or_2_out = REG_A | REG_B;  // OR_Gate or_2, 32 bits wide
  xor xor_2 (xor_2_out, REG_A[31], ACC_OUT[31]);
  and and_9 (FLAGS_OUT[1], xor_2_out, or_3_out);
  or or_3 (or_3_out, and_7_out, and_8_out);
  assign xor_3_out = REG_A ^ REG_B;  // XOR_Gate xor_3, 32 bits wide
  Shifter #(.width(32)) shifter_1 (.in(REG_A), .\dist (REG_B[4:0]), .out(shifter_1_out));
  Shifter #(.shift("lr"), .width(32)) shifter_2 (.in(REG_A), .\dist (REG_B[4:0]), .out(shifter_2_out));
  Shifter #(.shift("ar"), .width(32)) shifter_3 (.in(REG_A), .\dist (REG_B[4:0]), .out(shifter_3_out));
  Pull_Resistor pull_resistor_2 (.node({pull_resistor_2_node, FLAGS_OUT[31:4]}));
  Multiplexer #(.select(4), .width(32)) multiplexer_1 (
    .in0(add_32_1_output_bus_1), .in1(add_32_1_output_bus_1), .in2(multiplier_1_out), .in3(divider_1_out),
    .in4(and_6_out), .in5(or_2_out), .in6(xor_3_out), .in7(shifter_1_out), .in8(shifter_2_out),
    .in9(shifter_3_out), .out(ACC_OUT), .sel(OPCODE_SELECTOR));  // open: in10, in11, in12, in13, in14, in15
  not not_7 (not_7_out, OPCODE_SELECTOR[3]);
  not not_8 (not_8_out, OPCODE_SELECTOR[2]);
  not not_9 (not_9_out, OPCODE_SELECTOR[0]);
  and and_10 (and_10_out, not_7_out, not_8_out, OPCODE_SELECTOR[1], not_9_out);
  Multiplexer #(.width(32)) multiplexer_2 (
    .in0(divider_1_rem), .in1(multiplier_1_cout), .out(AUX_OUT), .sel(and_10_out));
  assign not_10_out = ~ACC_OUT;  // NOT_Gate not_10, 32 bits wide
  and and_11 (FLAGS_OUT[3], not_10_out[31], not_10_out[30], not_10_out[29], not_10_out[28], not_10_out[27], not_10_out[26], not_10_out[25], not_10_out[24], not_10_out[23], not_10_out[22], not_10_out[21], not_10_out[20], not_10_out[19], not_10_out[18], not_10_out[17], not_10_out[16], not_10_out[15], not_10_out[14], not_10_out[13], not_10_out[12], not_10_out[11], not_10_out[10], not_10_out[9], not_10_out[8], not_10_out[7], not_10_out[6], not_10_out[5], not_10_out[4], not_10_out[3], not_10_out[2], not_10_out[1], not_10_out[0]);

  assign FLAGS_OUT[2] = ACC_OUT[31];

  // Notes on the sheet:
  //   0 = Carry
  //   1 = Overflow
  //   2 = Sign
  //   3 = Zero
endmodule

module NOT_32 (
  input  [31:0] ACC_IN,
  output [31:0] ACC_OUT
);

  not not_1 (ACC_OUT[0], ACC_IN[0]);
  not not_2 (ACC_OUT[1], ACC_IN[1]);
  not not_3 (ACC_OUT[2], ACC_IN[2]);
  not not_4 (ACC_OUT[3], ACC_IN[3]);
  not not_5 (ACC_OUT[4], ACC_IN[4]);
  not not_6 (ACC_OUT[5], ACC_IN[5]);
  not not_7 (ACC_OUT[6], ACC_IN[6]);
  not not_8 (ACC_OUT[7], ACC_IN[7]);
  not not_9 (ACC_OUT[8], ACC_IN[8]);
  not not_10 (ACC_OUT[9], ACC_IN[9]);
  not not_11 (ACC_OUT[10], ACC_IN[10]);
  not not_12 (ACC_OUT[11], ACC_IN[11]);
  not not_13 (ACC_OUT[12], ACC_IN[12]);
  not not_14 (ACC_OUT[13], ACC_IN[13]);
  not not_15 (ACC_OUT[14], ACC_IN[14]);
  not not_16 (ACC_OUT[15], ACC_IN[15]);
  not not_17 (ACC_OUT[16], ACC_IN[16]);
  not not_18 (ACC_OUT[17], ACC_IN[17]);
  not not_19 (ACC_OUT[18], ACC_IN[18]);
  not not_20 (ACC_OUT[19], ACC_IN[19]);
  not not_21 (ACC_OUT[20], ACC_IN[20]);
  not not_22 (ACC_OUT[21], ACC_IN[21]);
  not not_23 (ACC_OUT[22], ACC_IN[22]);
  not not_24 (ACC_OUT[23], ACC_IN[23]);
  not not_25 (ACC_OUT[24], ACC_IN[24]);
  not not_26 (ACC_OUT[25], ACC_IN[25]);
  not not_27 (ACC_OUT[26], ACC_IN[26]);
  not not_28 (ACC_OUT[27], ACC_IN[27]);
  not not_29 (ACC_OUT[28], ACC_IN[28]);
  not not_30 (ACC_OUT[29], ACC_IN[29]);
  not not_31 (ACC_OUT[30], ACC_IN[30]);
  not not_32 (ACC_OUT[31], ACC_IN[31]);
endmodule

module Register_Page (
  input  [4:0] REG_READ_SELECTOR_A,
  input  [4:0] REG_READ_SELECTOR_B,
  input  CLK_IN,
  input  [31:0] REG_WRITE_DATA_IN,
  input  REG_WRITE_ENABLE,
  input  [4:0] REG_WRITE_SELECTOR,
  output [31:0] REG_READ_OUT_A,
  output [31:0] REG_READ_OUT_B
);

  wire demultiplexer_1_out0, demultiplexer_1_out1, demultiplexer_1_out2, demultiplexer_1_out3,
       demultiplexer_1_out4, demultiplexer_1_out5, demultiplexer_1_out6, demultiplexer_1_out7,
       demultiplexer_1_out8, demultiplexer_1_out9, demultiplexer_1_out10, demultiplexer_1_out11,
       demultiplexer_1_out12, demultiplexer_1_out13, demultiplexer_1_out14, demultiplexer_1_out15,
       demultiplexer_1_out16, demultiplexer_1_out17, demultiplexer_1_out18, demultiplexer_1_out19,
       demultiplexer_1_out20, demultiplexer_1_out21, demultiplexer_1_out22, demultiplexer_1_out23,
       demultiplexer_1_out24, demultiplexer_1_out25, demultiplexer_1_out26, demultiplexer_1_out27,
       demultiplexer_1_out28, demultiplexer_1_out29, demultiplexer_1_out30, demultiplexer_1_out31, undriven,
       undriven_2, undriven_3, undriven_4;
  wire [31:0] demultiplexer_2_out0, demultiplexer_2_out1, demultiplexer_2_out2, demultiplexer_2_out3,
       demultiplexer_2_out4, demultiplexer_2_out5, demultiplexer_2_out6, demultiplexer_2_out7,
       demultiplexer_2_out8, demultiplexer_2_out9, demultiplexer_2_out10, demultiplexer_2_out11,
       demultiplexer_2_out12, demultiplexer_2_out13, demultiplexer_2_out14, demultiplexer_2_out15,
       demultiplexer_2_out16, demultiplexer_2_out17, demultiplexer_2_out18, demultiplexer_2_out19,
       demultiplexer_2_out20, demultiplexer_2_out21, demultiplexer_2_out22, demultiplexer_2_out23,
       demultiplexer_2_out24, demultiplexer_2_out25, demultiplexer_2_out26, demultiplexer_2_out27,
       demultiplexer_2_out28, demultiplexer_2_out29, demultiplexer_2_out30, demultiplexer_2_out31, r0_q,
       r1_q, r2_q, r3_q, r4_q, r5_q, r6_q, r7_q, r8_q, r9_q, r10_q, r11_q, r12_q, r13_q, r14_q, r15_q, r16_q,
       r17_q, r18_q, r19_q, r20_q, r21_q, r22_q, r23_q, r24_q, r25_q, r26_q, r27_q, r28_q, r29_q, r30_q,
       r31_q;

  Register #(.width(32)) r0 (.D(demultiplexer_2_out0), .en(demultiplexer_1_out0), .clk(CLK_IN), .Q(r0_q));  // open: clr
  Register #(.width(32)) r1 (.D(demultiplexer_2_out1), .en(demultiplexer_1_out1), .clk(CLK_IN), .Q(r1_q));  // open: clr
  Register #(.width(32)) r2 (.D(demultiplexer_2_out2), .en(demultiplexer_1_out2), .clk(CLK_IN), .Q(r2_q));  // open: clr
  Register #(.width(32)) r3 (.D(demultiplexer_2_out3), .en(demultiplexer_1_out3), .clk(CLK_IN), .Q(r3_q));  // open: clr
  Register #(.width(32)) r4 (.D(demultiplexer_2_out4), .en(demultiplexer_1_out4), .clk(CLK_IN), .Q(r4_q));  // open: clr
  Register #(.width(32)) r5 (.D(demultiplexer_2_out5), .en(demultiplexer_1_out5), .clk(CLK_IN), .Q(r5_q));  // open: clr
  Register #(.width(32)) r6 (.D(demultiplexer_2_out6), .en(demultiplexer_1_out6), .clk(CLK_IN), .Q(r6_q));  // open: clr
  Register #(.width(32)) r7 (.D(demultiplexer_2_out7), .en(demultiplexer_1_out7), .clk(CLK_IN), .Q(r7_q));  // open: clr
  Register #(.width(32)) r8 (.D(demultiplexer_2_out8), .en(demultiplexer_1_out8), .clk(CLK_IN), .Q(r8_q));  // open: clr
  Register #(.width(32)) r9 (.D(demultiplexer_2_out9), .en(demultiplexer_1_out9), .clk(CLK_IN), .Q(r9_q));  // open: clr
  Register #(.width(32)) r10 (
    .D(demultiplexer_2_out10), .en(demultiplexer_1_out10), .clk(CLK_IN), .Q(r10_q));  // open: clr
  Register #(.width(32)) r11 (
    .D(demultiplexer_2_out11), .en(demultiplexer_1_out11), .clk(CLK_IN), .Q(r11_q), .clr(undriven));
  Register #(.width(32)) r12 (
    .D(demultiplexer_2_out12), .en(demultiplexer_1_out12), .clk(CLK_IN), .Q(r12_q), .clr(undriven_2));
  Register #(.width(32)) r13 (
    .D(demultiplexer_2_out13), .en(demultiplexer_1_out13), .clk(CLK_IN), .Q(r13_q), .clr(undriven_3));
  Register #(.width(32)) r14 (
    .D(demultiplexer_2_out14), .en(demultiplexer_1_out14), .clk(CLK_IN), .Q(r14_q), .clr(undriven_4));
  Register #(.width(32)) r15 (
    .D(demultiplexer_2_out15), .en(demultiplexer_1_out15), .clk(CLK_IN), .Q(r15_q));  // open: clr
  Demultiplexer #(.select(5)) demultiplexer_1 (
    .out0(demultiplexer_1_out0), .out1(demultiplexer_1_out1), .out2(demultiplexer_1_out2),
    .out3(demultiplexer_1_out3), .out4(demultiplexer_1_out4), .out5(demultiplexer_1_out5),
    .out6(demultiplexer_1_out6), .out7(demultiplexer_1_out7), .out8(demultiplexer_1_out8),
    .out9(demultiplexer_1_out9), .out10(demultiplexer_1_out10), .out11(demultiplexer_1_out11),
    .out12(demultiplexer_1_out12), .out13(demultiplexer_1_out13), .out14(demultiplexer_1_out14),
    .out15(demultiplexer_1_out15), .out16(demultiplexer_1_out16), .out17(demultiplexer_1_out17),
    .out18(demultiplexer_1_out18), .out19(demultiplexer_1_out19), .out20(demultiplexer_1_out20),
    .out21(demultiplexer_1_out21), .out22(demultiplexer_1_out22), .out23(demultiplexer_1_out23),
    .out24(demultiplexer_1_out24), .out25(demultiplexer_1_out25), .out26(demultiplexer_1_out26),
    .out27(demultiplexer_1_out27), .out28(demultiplexer_1_out28), .out29(demultiplexer_1_out29),
    .out30(demultiplexer_1_out30), .out31(demultiplexer_1_out31), .in(REG_WRITE_ENABLE),
    .sel(REG_WRITE_SELECTOR));
  Register #(.width(32)) r16 (
    .D(demultiplexer_2_out16), .en(demultiplexer_1_out16), .clk(CLK_IN), .Q(r16_q));  // open: clr
  Register #(.width(32)) r17 (
    .D(demultiplexer_2_out17), .en(demultiplexer_1_out17), .clk(CLK_IN), .Q(r17_q));  // open: clr
  Register #(.width(32)) r18 (
    .D(demultiplexer_2_out18), .en(demultiplexer_1_out18), .clk(CLK_IN), .Q(r18_q));  // open: clr
  Register #(.width(32)) r19 (
    .D(demultiplexer_2_out19), .en(demultiplexer_1_out19), .clk(CLK_IN), .Q(r19_q));  // open: clr
  Register #(.width(32)) r20 (
    .D(demultiplexer_2_out20), .en(demultiplexer_1_out20), .clk(CLK_IN), .Q(r20_q));  // open: clr
  Register #(.width(32)) r21 (
    .D(demultiplexer_2_out21), .en(demultiplexer_1_out21), .clk(CLK_IN), .Q(r21_q));  // open: clr
  Register #(.width(32)) r22 (
    .D(demultiplexer_2_out22), .en(demultiplexer_1_out22), .clk(CLK_IN), .Q(r22_q));  // open: clr
  Register #(.width(32)) r23 (
    .D(demultiplexer_2_out23), .en(demultiplexer_1_out23), .clk(CLK_IN), .Q(r23_q));  // open: clr
  Register #(.width(32)) r24 (
    .D(demultiplexer_2_out24), .en(demultiplexer_1_out24), .clk(CLK_IN), .Q(r24_q));  // open: clr
  Register #(.width(32)) r25 (
    .D(demultiplexer_2_out25), .en(demultiplexer_1_out25), .clk(CLK_IN), .Q(r25_q));  // open: clr
  Register #(.width(32)) r26 (
    .D(demultiplexer_2_out26), .en(demultiplexer_1_out26), .clk(CLK_IN), .Q(r26_q));  // open: clr
  Register #(.width(32)) r27 (
    .D(demultiplexer_2_out27), .en(demultiplexer_1_out27), .clk(CLK_IN), .Q(r27_q));  // open: clr
  Register #(.width(32)) r28 (
    .D(demultiplexer_2_out28), .en(demultiplexer_1_out28), .clk(CLK_IN), .Q(r28_q));  // open: clr
  Register #(.width(32)) r29 (
    .D(demultiplexer_2_out29), .en(demultiplexer_1_out29), .clk(CLK_IN), .Q(r29_q));  // open: clr
  Register #(.width(32)) r30 (
    .D(demultiplexer_2_out30), .en(demultiplexer_1_out30), .clk(CLK_IN), .Q(r30_q));  // open: clr
  Register #(.width(32)) r31 (
    .D(demultiplexer_2_out31), .en(demultiplexer_1_out31), .clk(CLK_IN), .Q(r31_q));  // open: clr
  Demultiplexer #(.select(5), .width(32)) demultiplexer_2 (
    .out0(demultiplexer_2_out0), .out1(demultiplexer_2_out1), .out2(demultiplexer_2_out2),
    .out3(demultiplexer_2_out3), .out4(demultiplexer_2_out4), .out5(demultiplexer_2_out5),
    .out6(demultiplexer_2_out6), .out7(demultiplexer_2_out7), .out8(demultiplexer_2_out8),
    .out9(demultiplexer_2_out9), .out10(demultiplexer_2_out10), .out11(demultiplexer_2_out11),
    .out12(demultiplexer_2_out12), .out13(demultiplexer_2_out13), .out14(demultiplexer_2_out14),
    .out15(demultiplexer_2_out15), .out16(demultiplexer_2_out16), .out17(demultiplexer_2_out17),
    .out18(demultiplexer_2_out18), .out19(demultiplexer_2_out19), .out20(demultiplexer_2_out20),
    .out21(demultiplexer_2_out21), .out22(demultiplexer_2_out22), .out23(demultiplexer_2_out23),
    .out24(demultiplexer_2_out24), .out25(demultiplexer_2_out25), .out26(demultiplexer_2_out26),
    .out27(demultiplexer_2_out27), .out28(demultiplexer_2_out28), .out29(demultiplexer_2_out29),
    .out30(demultiplexer_2_out30), .out31(demultiplexer_2_out31), .in(REG_WRITE_DATA_IN),
    .sel(REG_WRITE_SELECTOR));
  Multiplexer #(.select(5), .width(32)) multiplexer_1 (
    .in0(r0_q), .in1(r1_q), .in2(r2_q), .in3(r3_q), .in4(r4_q), .in5(r5_q), .in6(r6_q), .in7(r7_q),
    .in8(r8_q), .in9(r9_q), .in10(r10_q), .in11(r11_q), .in12(r12_q), .in13(r13_q), .in14(r14_q),
    .in15(r15_q), .in16(r16_q), .in17(r17_q), .in18(r18_q), .in19(r19_q), .in20(r20_q), .in21(r21_q),
    .in22(r22_q), .in23(r23_q), .in24(r24_q), .in25(r25_q), .in26(r26_q), .in27(r27_q), .in28(r28_q),
    .in29(r29_q), .in30(r30_q), .in31(r31_q), .out(REG_READ_OUT_A), .sel(REG_READ_SELECTOR_A));
  Multiplexer #(.select(5), .width(32)) multiplexer_2 (
    .in0(r0_q), .in1(r1_q), .in2(r2_q), .in3(r3_q), .in4(r4_q), .in5(r5_q), .in6(r6_q), .in7(r7_q),
    .in8(r8_q), .in9(r9_q), .in10(r10_q), .in11(r11_q), .in12(r12_q), .in13(r13_q), .in14(r14_q),
    .in15(r15_q), .in16(r16_q), .in17(r17_q), .in18(r18_q), .in19(r19_q), .in20(r20_q), .in21(r21_q),
    .in22(r22_q), .in23(r23_q), .in24(r24_q), .in25(r25_q), .in26(r26_q), .in27(r27_q), .in28(r28_q),
    .in29(r29_q), .in30(r30_q), .in31(r31_q), .out(REG_READ_OUT_B), .sel(REG_READ_SELECTOR_B));
endmodule

module Compare (
  input  [31:0] OP_1,
  input  [31:0] OP_2,
  input  [31:0] FLAGS_IN,
  output [31:0] FLAGS_OUT
);
endmodule

module MEM_SUBSYSTEM (
  input  [31:0] DATA_IN,
  input  [23:0] ADDR_IN,
  input  MEM_WRITE_ENABLE,
  input  QUADBYTE,
  input  CLK_IN,
  output [31:0] DATA_OUT
);

  wire pull_resistor_1_node;

  Pull_Resistor #(.pull(1)) pull_resistor_1 (.node(pull_resistor_1_node));
  // RAM #(.addrWidth(23), .enables("line"), .line("quad"), .misaligned("true")) ram_1: pin names not known; wires that end beside it: ADDR_IN[22:0], MEM_WRITE_ENABLE, pull_resistor_1_node, QUADBYTE, QUADBYTE, CLK_IN, DATA_IN[7:0], DATA_IN[15:8], DATA_IN[23:16], DATA_IN[31:24]
  Adder #(.width(24)) adder_1 ();  // open: a, b, out, cin, cout
endmodule

module CPU (
  input  PWR
);

  wire demultiplexer_1_out1, demultiplexer_1_out2, demultiplexer_1_out3, main_1_mem_write_enable,
       main_1_quadbyte, pull_resistor_1_node, ram_1_p7;
  wire [2:0] main_1_periph_addr_out;
  wire [6:0] keyboard_1_data;
  wire [7:0] ram_1_p12, ram_1_p14, ram_1_p15, rom_1_p2, rom_1_p3;
  wire [15:8] ram_1_p13;
  wire [21:0] rom_1_p1;
  wire [21:3] main_1_periph_addr_out_2;
  wire [22:0] main_1_mem_addr_out;
  wire [31:0] counter_1_q, main_1_mem_data_out, main_1_periph_data_out, multiplexer_1_out, multiplexer_2_out,
       multiplexer_3_out;
  wire [31:16] rom_1_p4;
  wire [31:31] pull_resistor_3_node;

  // ROM #(.addrWidth(22), .line("quad"), .misaligned("true")) rom_1: pin names not known; wires that end beside it: rom_1_p1, rom_1_p2, rom_1_p3, rom_1_p4[23:16], rom_1_p4[31:24]
  Multiplexer #(.width(32)) multiplexer_1 (
    .in0({{24{1'b0}}, rom_1_p2}), .in1({rom_1_p4, rom_1_p3, rom_1_p2}), .out(multiplexer_1_out),
    .sel(main_1_quadbyte));
  main main_1 (
    .CLK(ram_1_p7), .Power_button(PWR), .MEM_DATA_IN(multiplexer_3_out), .PERIPH_DATA_IN(multiplexer_2_out),
    .BOOT_ROM_DATA(multiplexer_1_out), .QUADBYTE(main_1_quadbyte),
    .PERIPH_ADDR_OUT({main_1_periph_addr_out_2, main_1_periph_addr_out}), .MEM_DATA_OUT(main_1_mem_data_out),
    .MEM_ADDR_OUT(main_1_mem_addr_out),
    .PERIPH_DATA_OUT({{25{main_1_periph_data_out[31]}}, main_1_periph_data_out[6:0]}),
    .BOOT_ROM_ADDR(rom_1_p1), .MEM_WRITE_ENABLE(main_1_mem_write_enable));
  Pull_Resistor #(.pull(1)) pull_resistor_1 (.node(pull_resistor_1_node));
  // RAM #(.addrWidth(23), .enables("line"), .line("quad"), .misaligned("true")) ram_1: pin names not known; wires that end beside it: main_1_mem_addr_out, main_1_mem_write_enable, pull_resistor_1_node, main_1_quadbyte, main_1_quadbyte, main_1_quadbyte, ram_1_p7, main_1_mem_data_out[7:0], main_1_mem_data_out[15:8], main_1_mem_data_out[23:16], main_1_mem_data_out[31:24], ram_1_p12, ram_1_p13, ram_1_p14, ram_1_p15
  Clock clock_1 (.out(ram_1_p7));
  Demultiplexer #(.select(3)) demultiplexer_1 (
    .out1(demultiplexer_1_out1), .out2(demultiplexer_1_out2), .out3(demultiplexer_1_out3), .in(1'b1),
    .sel(main_1_periph_addr_out));  // open: out0, out4, out5, out6, out7
  Pull_Resistor pull_resistor_2 (.node(main_1_periph_data_out[31]));
  LedBar #(.matrixcols(22), .persist(1)) ledbar_1 (
    .led0(main_1_periph_addr_out_2[21]), .led1(main_1_periph_addr_out_2[20]),
    .led2(main_1_periph_addr_out_2[19]), .led3(main_1_periph_addr_out_2[18]),
    .led4(main_1_periph_addr_out_2[17]), .led5(main_1_periph_addr_out_2[16]),
    .led6(main_1_periph_addr_out_2[15]), .led7(main_1_periph_addr_out_2[14]),
    .led8(main_1_periph_addr_out_2[13]), .led9(main_1_periph_addr_out_2[12]),
    .led10(main_1_periph_addr_out_2[11]), .led11(main_1_periph_addr_out_2[10]),
    .led12(main_1_periph_addr_out_2[9]), .led13(main_1_periph_addr_out_2[8]),
    .led14(main_1_periph_addr_out_2[7]), .led15(main_1_periph_addr_out_2[6]),
    .led16(main_1_periph_addr_out_2[5]), .led17(main_1_periph_addr_out_2[4]),
    .led18(main_1_periph_addr_out_2[3]), .led19(main_1_periph_addr_out[2]),
    .led20(main_1_periph_addr_out[1]), .led21(main_1_periph_addr_out[0]));
  Multiplexer #(.width(32)) multiplexer_2 (
    .in0({{25{pull_resistor_3_node[31]}}, keyboard_1_data}), .in1(counter_1_q), .out(multiplexer_2_out),
    .sel(demultiplexer_1_out3));
  Keyboard keyboard_1 (.clk(ram_1_p7), .re(demultiplexer_1_out2), .data(keyboard_1_data));  // open: clr, avail
  Pull_Resistor pull_resistor_3 (.node(pull_resistor_3_node[31]));
  Multiplexer #(.width(32)) multiplexer_3 (
    .in0({{24{1'b0}}, ram_1_p12}), .in1({ram_1_p15, ram_1_p14, ram_1_p13, ram_1_p12}),
    .out(multiplexer_3_out), .sel(main_1_quadbyte));
  TTY #(.cols(80), .rows(24)) tty_1 (
    .data(main_1_periph_data_out[6:0]), .clk(ram_1_p7), .we(demultiplexer_1_out1));  // open: clr
  Counter #(.max('hffffffff), .width(32)) counter_1 (
    .count(1'b1), .Q(counter_1_q), .up(1'b1), .clk(ram_1_p7));  // open: load, D, carry, clr

  // Notes on the sheet:
  //   contents of rom_1 (hex, n*v repeats v):
  //   13 0 0 0 68 d0 1 0 d1 ce 1 0 65 1 0 0 62 1 f0 ff 62 1 f8 ff 11 40 9d 2 62 e d0 ff e8 b 0 0 d1 4b 0 0
  //   65 8c 38 1 11 0 9d 2 62 e e8 ff 11 80 9b 2 62 e c8 ff e0 1 e8 ff 65 11 0 0 e7 21 0 0 60 1 f0 ff 34
  //   80 4 0 60 2 f8 ff 62 2 e0 ff 65 2 2 0 62 2 d8 ff 62 1 f0 ff 60 1 f0 ff 57 21 0 0 e0 1 e0 ff c0 21 0
  //   0 e0 3b 0 0 11 c0 30 2 e0 b d8 ff 11 c0 c 2 e0 1 e8 ff 60 1 f0 ff 50 11 0 0 67 31 0 0 34 80 fc f e4
  //   2b 0 0 d5 7b de 2 11 0 2b 2 60 1 d0 ff e0 b c8 ff c1 2b 0 0 11 40 2d 2 e5 ab 0 0 11 40 9 2 e8 e 0 0
  //   14 0 0 0 12 0 0 0 13 0 0 0 68 d0 1 0 d1 8e 4 0 e4 f6 ff ff 68 d1 0 0 55 1 fe ff e7 2b 0 0 38 40 1 0
  //   11 0 79 2 65 c1 0 0 62 c1 1 0 65 5 0 0 30 80 16 0 65 51 0 0 e7 2b 0 0 38 40 1 0 68 d1 0 0 55 81 ff
  //   ff d0 bb 0 0 c4 2b 0 0 30 40 0 0 e5 b 1 0 64 6 80 0 60 c2 0 0 68 41 0 0 54 11 0 0 65 7 0 0 67 e1 0 0
  //   e2 b f8 ff 32 40 5 0 65 1 0 0 67 22 0 0 32 80 1 0 62 6 d0 ff e2 6 80 ff 11 0 67 0 e0 6 80 ff 60 6 d0
  //   ff e0 b f8 ff d5 c6 ff ff 55 c6 2 0 60 c5 0 0 60 a1 8 0 44 d1 0 0 e8 71 1 0 d0 1 1 0 67 31 0 0 39 80
  //   b 0 11 0 86 0 68 c5 1 0 30 0 d 0 e7 4b 0 0 3a c0 2 0 e8 c1 0 0 d5 41 0 0 68 71 1 0 58 11 0 0 40 31 0
  //   0 60 25 f0 ff 67 e5 0 0 31 c0 0 0 e0 a1 10 0 e2 21 f0 ff 30 80 9 0 65 1 10 0 e7 2b 0 0 39 40 0 0 65
  //   17 0 0 65 f3 f 0 e7 6b 0 0 62 7 d8 ff 62 3 e0 ff 62 6 d0 ff 3a 40 8 0 e8 c1 0 0 d5 c1 2 0 68 71 1 0
  //   40 31 0 0 68 c2 0 0 55 42 3 0 e8 71 1 0 c0 41 0 0 60 35 8 0 67 25 0 0 31 80 9 0 68 a2 0 0 40 72 1 0
  //   e0 42 8 0 d5 12 0 0 60 a3 18 0 e2 42 8 0 62 33 8 0 62 61 10 0 30 0 2 0 e8 a1 0 0 c0 71 1 0 e2 c1 0 0
  //   41 71 1 0 d5 1b 0 0 e2 ab 8 0 55 11 0 0 62 31 8 0 50 85 0 0 68 ae 0 0 e8 e 0 0 14 0 0 0 12 0 0 0 e2
  //   6 80 ff 62 2 f0 ff 11 80 6c 0 62 e 70 ff e0 1 f0 ff d4 21 0 0 65 1 0 0 e7 21 0 0 32 40 0 0 30 40 0 0
  //   11 80 52 0 e0 b f8 ff 60 6 d0 ff 60 7 d8 ff 60 3 e0 ff 30 0 1 0 e2 6 80 ff 68 71 1 0 58 31 0 0 62 1
  //   70 ff 68 c8 0 0 55 8 4 0 60 5 1 0 e8 c7 0 0 d5 47 3 0 67 f5 0 0 31 0 21 0 68 71 1 0 50 1 1 0 62 1 78
  //   ff e5 3 0 0 65 14 0 0 e0 4 80 ff d5 c4 ff ff 60 1 d0 ff e8 21 0 0 d5 1 3 0 e2 1 c8 ff e8 25 0 0 d5
  //   c5 2 0 64 f6 ff 1f 55 c6 ff ff e8 26 0 0 d5 46 33 0 e2 7 90 ff 62 8 c0 ff e2 3 b8 ff 62 4 b0 ff e2 4
  //   a8 ff e2 5 88 ff 62 6 a0 ff e2 6 98 ff 30 0 6 0 68 c1 1 0 54 81 f 0 e8 21 0 0 c0 b1 0 0 40 f1 0 0 58
  //   3e 0 0 60 21 0 0 68 c2 1 0 54 f2 1 0 e8 82 0 0 c7 42 0 0 58 3e 0 0 44 ce 0 0 40 de 0 0 60 c2 1 0 45
  //   52 0 0 62 c2 1 0 62 a1 10 0 e2 a1 18 0 62 25 18 0 62 35 10 0 60 5 1 0 67 f5 0 0 31 80 14 0 60 a1 18
  //   0 67 f1 0 0 e8 81 0 0 31 40 0 0 e8 71 0 0 68 e2 0 0 44 32 0 0 60 ae 8 0 e8 c2 1 0 c4 92 0 0 54 12 0
  //   0 67 72 0 0 31 c0 1 0 e0 1 c8 ff e0 31 0 0 67 35 0 0 32 c0 0 0 e0 1 78 ff e7 32 0 0 3a 80 27 0 62 1
  //   1 0 e2 27 10 0 e7 72 1 0 31 0 25 0 67 6e 0 0 37 80 f3 f 62 5 f0 ff e8 5b 0 0 e2 2 e8 ff 11 80 52 0
  //   e0 5 88 ff e0 7 90 ff 68 c2 1 0 57 32 0 0 e8 41 0 0 c0 b1 0 0 40 f2 0 0 60 41 0 0 67 31 0 0 31 c0 4
  //   0 60 42 8 0 e0 42 8 0 60 3 e8 ff 67 53 0 0 60 7 d8 ff 60 8 c0 ff 60 5 f0 ff e0 3 b8 ff 60 4 b0 ff e0
  //   4 a8 ff 60 6 a0 ff e0 6 98 ff e8 62 0 0 39 0 4 0 68 31 0 0 e8 41 0 0 e0 b f8 ff 60 3 e0 ff 30 0 ed f
  //   e0 b f8 ff 60 7 d8 ff 60 8 c0 ff 60 5 f0 ff 60 3 e0 ff e0 3 b8 ff 60 4 b0 ff e0 4 a8 ff 60 6 a0 ff
  //   e0 6 98 ff 30 40 ea f d5 12 0 0 e0 21 8 0 e7 32 0 0 e0 b f8 ff 60 3 e0 ff 39 0 1 0 60 21 10 0 e0 21
  //   8 0 e7 32 0 0 38 0 ff f e0 21 18 0 30 40 e7 f 54 17 0 0 65 1 0 0 67 27 0 0 60 6 d0 ff e0 6 80 ff e0
  //   8 70 ff 32 40 5 0 e8 11 1 0 d7 31 0 0 68 c2 0 0 55 c2 2 0 e8 32 0 0 c0 42 0 0 68 c2 0 0 55 82 3 0 c0
  //   41 0 0 e0 31 0 0 e7 51 0 0 31 40 2 0 68 d3 0 0 55 c3 ff ff 60 32 8 0 44 62 0 0 67 72 1 0 39 c0 16 0
  //   e0 31 18 0 e7 51 0 0 32 40 fe f d0 18 0 0 68 12 1 0 54 f2 1 0 e5 11 0 0 68 34 0 0 47 44 0 0 68 c2 0
  //   0 55 c2 2 0 e8 13 1 0 d7 33 0 0 c0 43 0 0 e8 c2 0 0 d5 42 33 0 d8 58 0 0 68 13 1 0 57 23 0 0 40 53 0
  //   0 e0 64 0 0 68 d3 0 0 55 f3 ff ff 68 85 0 0 40 65 0 0 67 95 0 0 39 40 0 0 30 40 3 0 e7 38 0 0 3a 80
  //   b9 f d0 18 0 0 e8 13 1 0 d7 23 0 0 c0 53 0 0 e0 74 0 0 e7 24 0 0 31 c0 fd f e8 13 1 0 d7 83 0 0 c0
  //   43 0 0 68 34 0 0 68 85 0 0 44 95 0 0 67 25 0 0 31 40 0 0 30 80 1 0 57 14 0 0 68 85 0 0 44 95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
endmodule

module MMU (
  input  CLK_IN,
  input  [1:0] bytes,
  input  RESET_MMU,
  input  Write_in,
  input  [7:0] MEM_DATA_IN,
  input  [22:0] MEM_BYTE_ADDR,
  input  [31:0] CORE_DATA_IN,
  output [31:0] CORE_DATA_OUT,
  output MEM_OP_DONE_OUT,
  output MEM_WRITE_ENABLE,
  output [22:0] MEM_ADDR_OUT,
  output [7:0] MEM_DATA_OUT
);

  wire pull_resistor_1_node, shift_register_1_p1;
  wire [1:0] counter_2_q, subtractor_1_out, xnor_1_out;

  Counter #(.max('h3), .width(2)) counter_1 ();  // open: load, D, count, Q, carry, up, clk, clr
  Pull_Resistor #(.pull(1)) pull_resistor_1 (.node(pull_resistor_1_node));
  Counter #(.max('h3), .width(2)) counter_2 (
    .load(RESET_MMU), .D(2'b00), .count(shift_register_1_p1), .Q(counter_2_q), .up(pull_resistor_1_node),
    .clk(CLK_IN));  // open: carry, clr
  // Shift_Register #(.length(4), .width(8)) shift_register_1: pin names not known; wires that end beside it: shift_register_1_p1, CLK_IN, MEM_DATA_IN, CORE_DATA_OUT[7:0], CORE_DATA_OUT[15:8], CORE_DATA_OUT[23:16], CORE_DATA_OUT[31:24]
  not not_1 (shift_register_1_p1, MEM_OP_DONE_OUT);
  Subtractor #(.width(2)) subtractor_1 (.a(counter_2_q), .b(bytes), .out(subtractor_1_out));  // open: bin, bout
  Multiplexer #(.select(2), .width(8)) multiplexer_1 (
    .in0(CORE_DATA_IN[7:0]), .in1(CORE_DATA_IN[15:8]), .in2(CORE_DATA_IN[23:16]), .in3(CORE_DATA_IN[31:24]),
    .out(MEM_DATA_OUT));  // open: sel
  Adder #(.width(23)) adder_1 (
    .a({{21{1'b0}}, counter_2_q}), .b(MEM_BYTE_ADDR), .out(MEM_ADDR_OUT));  // open: cin, cout
  assign xnor_1_out = ~(2'b00 ^ subtractor_1_out);  // XNOR_Gate xnor_1, 2 bits wide
  and and_1 (MEM_OP_DONE_OUT, xnor_1_out[0], xnor_1_out[1]);

  assign MEM_WRITE_ENABLE = Write_in;
endmodule

module hw_adder_32 (
  input  [31:0] Operand_A,
  input  [31:0] Operand_B
);
endmodule
